// Logisim project main.circ as structural Verilog: 19 circuits, main circuit main
module main (
);

  wire abst_obj_1_drawing, and_1_out, and_2_out, and_3_out, clock_1_out, clock_2_out, clock_3_out,
       clock_4_out, cmd_draw, cmd_show, comparator_3_eq, comparator_4_eq, counter_1_carry, drawing, e_hold,
       e_i_hold, e_resume, hold, not_1_out, not_2_out, not_3_out, not_4_out, not_5_out, or_4_out, p_resume,
       p_write, pull_resistor_1_node, register_1_q, register_2_q, write, xor_1_out;
  wire [1:0] counter_3_q;
  wire [2:0] joystick_1_x, joystick_1_y;
  wire [4:0] abst_obj_1_cur_line, counter_1_q;
  wire [5:5] abst_obj_1_cur_line_2;
  wire [6:0] adder_2_out, adder_3_out, bit_extender_6_out, bit_extender_7_out, multiplexer_1_out,
       subtractor_1_out, subtractor_2_out, transistor_10_out, x, y;
  wire [15:0] adder_1_out, adder_4_out, bit_extender_1_out, bit_extender_5_out, id, mem_adr, mem_inp,
       multiplier_1_out, multiplier_2_out, over_cmd, over_id, over_x, over_y, ptr, transistor_2_out,
       transistor_4_out, transistor_6_out, transistor_8_out, undriven, undriven_2, undriven_3;
  wire [31:0] abst_obj_1_line_x1, abst_obj_1_line_x2, n32video_buffer_extendable_1_out_5,
       n32video_buffer_extendable_1_out_6, n32video_buffer_extendable_1_out_7,
       n32video_buffer_extendable_1_out_8, n32video_buffer_extendable_1_out_9,
       n32video_buffer_extendable_1_out_10, n32video_buffer_extendable_1_out_11,
       n32video_buffer_extendable_1_out_12, n32video_buffer_extendable_1_out_13,
       n32video_buffer_extendable_1_out_14, n32video_buffer_extendable_1_out_15,
       n32video_buffer_extendable_1_out_16, n32video_buffer_extendable_1_out_17,
       n32video_buffer_extendable_1_out_18, n32video_buffer_extendable_1_out_19,
       n32video_buffer_extendable_1_out_20, n32video_buffer_extendable_1_out_21,
       n32video_buffer_extendable_1_out_22, n32video_buffer_extendable_1_out_23,
       n32video_buffer_extendable_1_out_24, n32video_buffer_extendable_1_out_25,
       n32video_buffer_extendable_1_out_26, n32video_buffer_extendable_1_out_27,
       n32video_buffer_extendable_1_out_28, n32video_buffer_extendable_1_out_29,
       n32video_buffer_extendable_1_out_30, n32video_buffer_extendable_1_out_31,
       n32video_buffer_extendable_1_out_32, n32video_buffer_extendable_1_out_33,
       n32video_buffer_extendable_1_out_34, n32video_buffer_extendable_1_out_35,
       n32video_buffer_extendable_1_out_36, rom_2_data;

  abst_obj abst_obj_1 (
    .y(y), .texture_line(counter_1_q), .write(xor_1_out), .texture_input(rom_2_data), .draw(counter_1_carry),
    .cur_line({abst_obj_1_cur_line_2[5], abst_obj_1_cur_line}), .line_x1(abst_obj_1_line_x1),
    .line_x2(abst_obj_1_line_x2), .x(x), .drawing(abst_obj_1_drawing));
  Counter #(.width(5), .max('h3)) counter_1 (
    .Q(counter_1_q), .carry(counter_1_carry), .clk(pull_resistor_1_node), .clr(counter_1_carry));  // open: load, D, count
  Pull_Resistor pull_resistor_1 (.node(pull_resistor_1_node));
  Transistor #(.\type ("n"), .gate("br")) transistor_1 (
    .in(clock_1_out), .out(pull_resistor_1_node), .gate(register_2_q));
  Clock clock_1 (.out(clock_1_out));
  xor xor_1 (xor_1_out, pull_resistor_1_node, register_2_q);
  Register #(.width(1)) register_1 (
    .D(and_1_out), .Q(register_1_q), .clk(and_1_out), .clr(abst_obj_1_drawing));  // open: en
  not not_1 (not_1_out, clock_2_out);
  Clock clock_2 (.out(clock_2_out));
  Register #(.width(1)) register_2 (
    .D(register_1_q), .Q(register_2_q), .clk(not_1_out), .clr(abst_obj_1_drawing));  // open: en
  or or_1 (drawing, register_2_q, register_1_q, abst_obj_1_drawing);
  ROM #(.addrWidth(16)) rom_1 ();  // open: addr, data, sel
  Clock clock_3 (.out(clock_3_out));
  assign bit_extender_1_out = {{11{1'b0}}, counter_1_q};  // Bit_Extender bit_extender_1
  Transistor #(.\type ("n"), .width(16)) transistor_2 (.in(over_id), .out(transistor_2_out), .gate(e_hold));
  Transistor #(.gate("br"), .width(16)) transistor_3 (.in(id), .out(transistor_2_out), .gate(e_hold));
  Transistor #(.width(16)) transistor_4 (.in(undriven), .out(transistor_4_out), .gate(e_hold));
  Transistor #(.\type ("n"), .width(16)) transistor_5 (.in(over_x), .out(transistor_4_out), .gate(e_hold));
  Transistor #(.width(16)) transistor_6 (.in(undriven_2), .out(transistor_6_out), .gate(e_hold));
  Transistor #(.\type ("n"), .width(16)) transistor_7 (.in(over_y), .out(transistor_6_out), .gate(e_hold));
  Transistor #(.\type ("n"), .width(16)) transistor_8 (.in(over_cmd), .out(transistor_8_out), .gate(e_hold));
  Transistor #(.gate("br"), .width(16)) transistor_9 (.in(undriven_3), .out(transistor_8_out), .gate(e_hold));
  // Probe on {abst_obj_1_cur_line_2[5], abst_obj_1_cur_line}
  // Probe on transistor_2_out
  Bit_Extender #(.in_width(16), .out_width(7)) bit_extender_2 (.in(transistor_4_out), .out(x));
  Bit_Extender #(.in_width(16), .out_width(7)) bit_extender_3 (.in(transistor_6_out), .out(y));
  // Probe on transistor_8_out
  Adder #(.width(16)) adder_1 (.a(bit_extender_1_out), .b(multiplier_1_out), .out(adder_1_out));  // open: cin, cout
  Multiplier #(.width(16)) multiplier_1 (.a(transistor_2_out), .b(16'h3), .out(multiplier_1_out));  // open: cin, cout
  // Probe on x
  // Probe on y
  Comparator #(.width(16), .mode("unsigned")) comparator_1 (
    .a(transistor_8_out), .b(16'h1), .eq(cmd_draw));  // open: gt, lt
  Comparator #(.width(16), .mode("unsigned")) comparator_2 (
    .a(transistor_8_out), .b(16'h2), .eq(cmd_show));  // open: gt, lt
  not not_2 (not_2_out, abst_obj_1_cur_line_2[5]);
  ROM #(.addrWidth(16), .dataWidth(32)) rom_2 (.addr(adder_1_out), .data(rom_2_data));  // open: sel
  not not_3 (not_3_out, write);
  and and_1 (and_1_out, cmd_draw, not_3_out);
  Comparator #(.width(16), .mode("unsigned")) comparator_3 (.a(id), .b(16'h2), .eq(comparator_3_eq));  // open: gt, lt
  buf or_2 (write, p_write);  // OR_Gate
  Comparator #(.width(16), .mode("unsigned")) comparator_4 (
    .a(id), .b({16{1'b0}}), .eq(comparator_4_eq));  // open: gt, lt
  and and_2 (and_2_out, comparator_4_eq, cmd_draw);
  and and_3 (and_3_out, comparator_3_eq, cmd_draw);
  enemies enemies_1 (
    .\wait (drawing), .draw(e_hold), .id(over_id), .y(over_x), .x(over_y), .command(over_cmd),
    .ready(e_resume), .initing(e_i_hold));  // open: collide, clock, DEBUG__enemy_cout
  or or_3 (hold, e_i_hold, e_hold);
  Counter #(.width(1), .max('h1)) counter_2 (
    .Q(p_write), .clk(and_2_out), .clr(p_resume));  // open: load, D, count, carry
  Register #(.width(1)) register_3 (.D(and_3_out), .Q(e_hold), .clk(and_3_out), .clr(e_resume));  // open: en
  DotMatrix #(.inputtype("row"), .matrixcols(32), .matrixrows(32)) dotmatrix_1 (
    .row0(n32video_buffer_extendable_1_out_5), .row1(n32video_buffer_extendable_1_out_6),
    .row2(n32video_buffer_extendable_1_out_7), .row3(n32video_buffer_extendable_1_out_8),
    .row4(n32video_buffer_extendable_1_out_9), .row5(n32video_buffer_extendable_1_out_10),
    .row6(n32video_buffer_extendable_1_out_11), .row7(n32video_buffer_extendable_1_out_12),
    .row8(n32video_buffer_extendable_1_out_13), .row9(n32video_buffer_extendable_1_out_14),
    .row10(n32video_buffer_extendable_1_out_15), .row11(n32video_buffer_extendable_1_out_16),
    .row12(n32video_buffer_extendable_1_out_17), .row13(n32video_buffer_extendable_1_out_18),
    .row14(n32video_buffer_extendable_1_out_19), .row15(n32video_buffer_extendable_1_out_20),
    .row16(n32video_buffer_extendable_1_out_21), .row17(n32video_buffer_extendable_1_out_22),
    .row18(n32video_buffer_extendable_1_out_23), .row19(n32video_buffer_extendable_1_out_24),
    .row20(n32video_buffer_extendable_1_out_25), .row21(n32video_buffer_extendable_1_out_26),
    .row22(n32video_buffer_extendable_1_out_27), .row23(n32video_buffer_extendable_1_out_28),
    .row24(n32video_buffer_extendable_1_out_29), .row25(n32video_buffer_extendable_1_out_30),
    .row26(n32video_buffer_extendable_1_out_31), .row27(n32video_buffer_extendable_1_out_32),
    .row28(n32video_buffer_extendable_1_out_33), .row29(n32video_buffer_extendable_1_out_34),
    .row30(n32video_buffer_extendable_1_out_35), .row31(n32video_buffer_extendable_1_out_36));
  _32video_buffer_extendable u_32video_buffer_extendable_1 (
    .in_1(abst_obj_1_line_x1), .out_5(n32video_buffer_extendable_1_out_5),
    .out_6(n32video_buffer_extendable_1_out_6), .out_7(n32video_buffer_extendable_1_out_7),
    .out_8(n32video_buffer_extendable_1_out_8), .out_9(n32video_buffer_extendable_1_out_9),
    .out_10(n32video_buffer_extendable_1_out_10), .out_11(n32video_buffer_extendable_1_out_11),
    .out_12(n32video_buffer_extendable_1_out_12), .out_13(n32video_buffer_extendable_1_out_13),
    .out_14(n32video_buffer_extendable_1_out_14), .out_15(n32video_buffer_extendable_1_out_15),
    .out_16(n32video_buffer_extendable_1_out_16), .out_17(n32video_buffer_extendable_1_out_17),
    .out_18(n32video_buffer_extendable_1_out_18), .out_19(n32video_buffer_extendable_1_out_19),
    .out_20(n32video_buffer_extendable_1_out_20), .out_21(n32video_buffer_extendable_1_out_21),
    .out_22(n32video_buffer_extendable_1_out_22), .out_23(n32video_buffer_extendable_1_out_23),
    .out_24(n32video_buffer_extendable_1_out_24), .out_25(n32video_buffer_extendable_1_out_25),
    .out_26(n32video_buffer_extendable_1_out_26), .out_27(n32video_buffer_extendable_1_out_27),
    .out_28(n32video_buffer_extendable_1_out_28), .out_29(n32video_buffer_extendable_1_out_29),
    .out_30(n32video_buffer_extendable_1_out_30), .out_31(n32video_buffer_extendable_1_out_31),
    .out_32(n32video_buffer_extendable_1_out_32), .out_33(n32video_buffer_extendable_1_out_33),
    .out_34(n32video_buffer_extendable_1_out_34), .out_35(n32video_buffer_extendable_1_out_35),
    .out_36(n32video_buffer_extendable_1_out_36), .block(not_4_out), .y(abst_obj_1_cur_line), .w(cmd_show));
  not not_4 (not_4_out, not_2_out);
  Transistor #(.\type ("n"), .width(7)) transistor_10 (.in(multiplexer_1_out), .out(transistor_10_out), .gate(p_write));
  Counter #(.width(2), .max('h3)) counter_3 (
    .Q(counter_3_q), .carry(p_resume), .clk(clock_4_out), .clr(or_4_out));  // open: load, D, count
  Clock clock_4 (.out(clock_4_out));
  or or_4 (or_4_out, not_5_out, p_resume);
  not not_5 (not_5_out, p_write);
  Multiplexer #(.select(2), .width(7), .enable("false")) multiplexer_1 (
    .in0({7{1'b0}}), .in1(adder_2_out), .in2(adder_3_out), .out(multiplexer_1_out), .sel(counter_3_q));  // open: in3
  assign mem_inp = {{9{1'b0}}, transistor_10_out};  // Bit_Extender bit_extender_4
  // Probe on adder_2_out
  // Probe on adder_3_out
  assign bit_extender_5_out = {{14{1'b0}}, counter_3_q};  // Bit_Extender bit_extender_5
  Joystick #(.bits(3)) joystick_1 (.x(joystick_1_x), .y(joystick_1_y));
  assign bit_extender_6_out = {{4{1'b0}}, joystick_1_x};  // Bit_Extender bit_extender_6
  Subtractor #(.width(7)) subtractor_1 (
    .a(bit_extender_6_out), .b(7'b0000100), .out(subtractor_1_out));  // open: bin, bout
  assign bit_extender_7_out = {{4{1'b0}}, joystick_1_y};  // Bit_Extender bit_extender_7
  Subtractor #(.width(7)) subtractor_2 (
    .a(bit_extender_7_out), .b(7'b0000100), .out(subtractor_2_out));  // open: bin, bout
  Multiplier #(.width(16)) multiplier_2 (.a(bit_extender_5_out), .b(16'h2), .out(multiplier_2_out));  // open: cin, cout
  Adder #(.width(7)) adder_2 (.a(x), .b(subtractor_1_out), .out(adder_2_out));  // open: cin, cout
  Adder #(.width(7)) adder_3 (.a(y), .b(subtractor_2_out), .out(adder_3_out));  // open: cin, cout
  // Probe on multiplier_2_out
  Adder #(.width(16)) adder_4 (.a(multiplier_2_out), .b(ptr), .out(adder_4_out));  // open: cin, cout
  Transistor #(.\type ("n"), .width(16)) transistor_11 (.in(adder_4_out), .out(mem_adr), .gate(p_write));

  // Other names for the same wires on the sheet: multi_obj_draw = e_hold

  // Notes on the sheet:
  //   texture line counter
  //   level data
  //   contents of rom_2 (hex, n*v repeats v):
  //   2 7 5 2 5 5 0 0 0 2 7 5 2 5 5 7 5 5 2 7 7 2 5 7 2 5 5
endmodule

module _32buffer_el (
  input  [31:0] \input ,
  input  _1___buffer_read,
  input  _1___buffer_write___clr,
  output [31:0] video,
  output [31:0] out_5
);

  wire [31:0] or_1_out;

  assign or_1_out = \input  | out_5;  // OR_Gate or_1, 32 bits wide
  Register #(.width(32)) buffer (
    .D(or_1_out), .Q(out_5), .clk(_1___buffer_read), .clr(_1___buffer_write___clr));  // open: en
  Register #(.width(32)) u_video (.D(out_5), .Q(video), .clk(_1___buffer_write___clr));  // open: en, clr
endmodule

module _32video_buffer_extendable (
  input  [31:0] in_1,
  input  w,
  input  block,
  input  [4:0] y,
  output [31:0] out_5,
  output [31:0] out_6,
  output [31:0] out_7,
  output [31:0] out_8,
  output [31:0] out_9,
  output [31:0] out_10,
  output [31:0] out_11,
  output [31:0] out_12,
  output [31:0] out_13,
  output [31:0] out_14,
  output [31:0] out_15,
  output [31:0] out_16,
  output [31:0] out_17,
  output [31:0] out_18,
  output [31:0] out_19,
  output [31:0] out_20,
  output [31:0] out_21,
  output [31:0] out_22,
  output [31:0] out_23,
  output [31:0] out_24,
  output [31:0] out_25,
  output [31:0] out_26,
  output [31:0] out_27,
  output [31:0] out_28,
  output [31:0] out_29,
  output [31:0] out_30,
  output [31:0] out_31,
  output [31:0] out_32,
  output [31:0] out_33,
  output [31:0] out_34,
  output [31:0] out_35,
  output [31:0] out_36
);

  wire _0, _1, _2, _3, _4, _5, _6, _7, _8, _9, _10, _11, _12, _13, _14, _15, _16, _17, _18, _19, _20, _21,
       _22, _23, _24, _25, _26, _27, _28, _29, _30, _31, clock_1_out, nor_1_out;
  wire [31:0] r0, r1, r2, r3, r4, r5, r6, r7, r8, r9, r10, r11, r12, r13, r14, r15, r16, r17, r18, r19, r20,
       r21, r22, r23, r24, r25, r26, r27, r28, r29, r30, r31;

  Demultiplexer #(.select(5), .disabled(0)) demultiplexer_1 (
    .out0(_0), .out1(_1), .out2(_2), .out3(_3), .out4(_4), .out5(_5), .out6(_6), .out7(_7), .out8(_8),
    .out9(_9), .out10(_10), .out11(_11), .out12(_12), .out13(_13), .out14(_14), .out15(_15), .out16(_16),
    .out17(_17), .out18(_18), .out19(_19), .out20(_20), .out21(_21), .out22(_22), .out23(_23), .out24(_24),
    .out25(_25), .out26(_26), .out27(_27), .out28(_28), .out29(_29), .out30(_30), .out31(_31), .in(1'b1),
    .sel(y), .en(nor_1_out));
  nor nor_1 (nor_1_out, block, clock_1_out);
  Clock clock_1 (.out(clock_1_out));
  _32buffer_el u_32buffer_el_1 (
    .\input (in_1), ._1___buffer_read(_0), .out_5(r0), .video(out_5), ._1___buffer_write___clr(w));
  _32buffer_el u_32buffer_el_2 (
    .\input (in_1), ._1___buffer_read(_1), .out_5(r1), .video(out_6), ._1___buffer_write___clr(w));
  _32buffer_el u_32buffer_el_3 (
    .\input (in_1), ._1___buffer_read(_2), .out_5(r2), .video(out_7), ._1___buffer_write___clr(w));
  _32buffer_el u_32buffer_el_4 (
    .\input (in_1), ._1___buffer_read(_3), .out_5(r3), .video(out_8), ._1___buffer_write___clr(w));
  _32buffer_el u_32buffer_el_5 (
    .\input (in_1), ._1___buffer_read(_4), .out_5(r4), .video(out_9), ._1___buffer_write___clr(w));
  _32buffer_el u_32buffer_el_6 (
    .\input (in_1), ._1___buffer_read(_5), .out_5(r5), .video(out_10), ._1___buffer_write___clr(w));
  _32buffer_el u_32buffer_el_7 (
    .\input (in_1), ._1___buffer_read(_6), .out_5(r6), .video(out_11), ._1___buffer_write___clr(w));
  _32buffer_el u_32buffer_el_8 (
    .\input (in_1), ._1___buffer_read(_7), .out_5(r7), .video(out_12), ._1___buffer_write___clr(w));
  _32buffer_el u_32buffer_el_9 (
    .\input (in_1), ._1___buffer_read(_8), .out_5(r8), .video(out_13), ._1___buffer_write___clr(w));
  _32buffer_el u_32buffer_el_10 (
    .\input (in_1), ._1___buffer_read(_9), .out_5(r9), .video(out_14), ._1___buffer_write___clr(w));
  _32buffer_el u_32buffer_el_11 (
    .\input (in_1), ._1___buffer_read(_10), .out_5(r10), .video(out_15), ._1___buffer_write___clr(w));
  _32buffer_el u_32buffer_el_12 (
    .\input (in_1), ._1___buffer_read(_11), .out_5(r11), .video(out_16), ._1___buffer_write___clr(w));
  _32buffer_el u_32buffer_el_13 (
    .\input (in_1), ._1___buffer_read(_12), .out_5(r12), .video(out_17), ._1___buffer_write___clr(w));
  _32buffer_el u_32buffer_el_14 (
    .\input (in_1), ._1___buffer_read(_13), .out_5(r13), .video(out_18), ._1___buffer_write___clr(w));
  _32buffer_el u_32buffer_el_15 (
    .\input (in_1), ._1___buffer_read(_14), .out_5(r14), .video(out_19), ._1___buffer_write___clr(w));
  _32buffer_el u_32buffer_el_16 (
    .\input (in_1), ._1___buffer_read(_15), .out_5(r15), .video(out_20), ._1___buffer_write___clr(w));
  _32buffer_el u_32buffer_el_17 (
    .\input (in_1), ._1___buffer_read(_16), .out_5(r16), .video(out_21), ._1___buffer_write___clr(w));
  _32buffer_el u_32buffer_el_18 (
    .\input (in_1), ._1___buffer_read(_17), .out_5(r17), .video(out_22), ._1___buffer_write___clr(w));
  _32buffer_el u_32buffer_el_19 (
    .\input (in_1), ._1___buffer_read(_18), .out_5(r18), .video(out_23), ._1___buffer_write___clr(w));
  _32buffer_el u_32buffer_el_20 (
    .\input (in_1), ._1___buffer_read(_19), .out_5(r19), .video(out_24), ._1___buffer_write___clr(w));
  _32buffer_el u_32buffer_el_21 (
    .\input (in_1), ._1___buffer_read(_20), .out_5(r20), .video(out_25), ._1___buffer_write___clr(w));
  _32buffer_el u_32buffer_el_22 (
    .\input (in_1), ._1___buffer_read(_21), .out_5(r21), .video(out_26), ._1___buffer_write___clr(w));
  _32buffer_el u_32buffer_el_23 (
    .\input (in_1), ._1___buffer_read(_22), .out_5(r22), .video(out_27), ._1___buffer_write___clr(w));
  _32buffer_el u_32buffer_el_24 (
    .\input (in_1), ._1___buffer_read(_23), .out_5(r23), .video(out_28), ._1___buffer_write___clr(w));
  _32buffer_el u_32buffer_el_25 (
    .\input (in_1), ._1___buffer_read(_24), .out_5(r24), .video(out_29), ._1___buffer_write___clr(w));
  _32buffer_el u_32buffer_el_26 (
    .\input (in_1), ._1___buffer_read(_25), .out_5(r25), .video(out_30), ._1___buffer_write___clr(w));
  _32buffer_el u_32buffer_el_27 (
    .\input (in_1), ._1___buffer_read(_26), .out_5(r26), .video(out_31), ._1___buffer_write___clr(w));
  _32buffer_el u_32buffer_el_28 (
    .\input (in_1), ._1___buffer_read(_27), .out_5(r27), .video(out_32), ._1___buffer_write___clr(w));
  _32buffer_el u_32buffer_el_29 (
    .\input (in_1), ._1___buffer_read(_28), .out_5(r28), .video(out_33), ._1___buffer_write___clr(w));
  _32buffer_el u_32buffer_el_30 (
    .\input (in_1), ._1___buffer_read(_29), .out_5(r29), .video(out_34), ._1___buffer_write___clr(w));
  _32buffer_el u_32buffer_el_31 (
    .\input (in_1), ._1___buffer_read(_30), .out_5(r30), .video(out_35), ._1___buffer_write___clr(w));
  _32buffer_el u_32buffer_el_32 (
    .\input (in_1), ._1___buffer_read(_31), .out_5(r31), .video(out_36), ._1___buffer_write___clr(w));

  // Other names for the same wires on the sheet: inp[31:0] = in_1

  // Notes on the sheet:
  //   block: pull=down
endmodule

module _32x32_ball (
  input  [5:0] in_1,
  input  [5:0] in_2,
  input  in_3,
  input  [4:0] in_4,
  output [31:0] out_5
);

  wire and_1_out, and_2_out, and_3_out, clock_1_out, clock_2_out, counter_1_q, counter_2_q, nor_1_out,
       nor_2_out, or_1_out, or_2_out;
  wire [4:0] bit_extender_1_out, bit_extender_2_out, xnor_1_out;
  wire [5:0] adder_1_out, adder_2_out, negator_1_out, negator_2_out, transistor_1_out, transistor_3_out, x_q,
       xv_q, y_q, yv_q;
  wire [31:0] shifter_1_out;

  // Probe on in_1
  // Probe on in_2
  Negator #(.width(6)) negator_1 (.in(in_1), .out(negator_1_out));
  Transistor #(.\type ("n"), .gate("br"), .width(6)) transistor_1 (
    .in(negator_1_out), .out(transistor_1_out), .gate(counter_2_q));
  Transistor #(.width(6)) transistor_2 (.in(in_1), .out(transistor_1_out), .gate(counter_2_q));
  Negator #(.width(6)) negator_2 (.in(in_2), .out(negator_2_out));
  Transistor #(.\type ("n"), .gate("br"), .width(6)) transistor_3 (
    .in(negator_2_out), .out(transistor_3_out), .gate(counter_1_q));
  Transistor #(.width(6)) transistor_4 (.in(in_2), .out(transistor_3_out), .gate(counter_1_q));
  Counter #(.width(1), .max('h1)) counter_1 (.Q(counter_1_q), .clk(or_1_out));  // open: load, D, count, carry, clr
  or or_1 (or_1_out, and_2_out, nor_1_out);
  nor nor_1 (nor_1_out, bit_extender_2_out[0], bit_extender_2_out[1], bit_extender_2_out[2], bit_extender_2_out[3], bit_extender_2_out[4]);
  Counter #(.width(1), .max('h1)) counter_2 (.Q(counter_2_q), .clk(or_2_out));  // open: load, D, count, carry, clr
  and and_1 (and_1_out, bit_extender_1_out[0], bit_extender_1_out[1], bit_extender_1_out[2], bit_extender_1_out[3], bit_extender_1_out[4]);
  or or_2 (or_2_out, and_1_out, nor_2_out);
  nor nor_2 (nor_2_out, bit_extender_1_out[0], bit_extender_1_out[1], bit_extender_1_out[2], bit_extender_1_out[3], bit_extender_1_out[4]);
  Register #(.width(6)) xv (.D(transistor_1_out), .Q(xv_q), .clk(clock_1_out));  // open: en, clr
  Clock clock_1 (.out(clock_1_out));
  Register #(.width(6)) yv (.D(transistor_3_out), .Q(yv_q), .clk(clock_2_out));  // open: en, clr
  Clock clock_2 (.out(clock_2_out));
  and and_2 (and_2_out, bit_extender_2_out[0], bit_extender_2_out[1], bit_extender_2_out[2], bit_extender_2_out[3], bit_extender_2_out[4]);
  Adder #(.width(6)) adder_1 (.a(xv_q), .b(x_q), .out(adder_1_out));  // open: cin, cout
  Adder #(.width(6)) adder_2 (.a(yv_q), .b(y_q), .out(adder_2_out));  // open: cin, cout
  Register #(.width(6)) x (.D(adder_1_out), .Q(x_q), .clk(in_3));  // open: en, clr
  Register #(.width(6)) y (.D(adder_2_out), .Q(y_q), .clk(in_3));  // open: en, clr
  Bit_Extender #(.in_width(6), .out_width(5)) bit_extender_1 (.in(x_q), .out(bit_extender_1_out));
  Bit_Extender #(.in_width(6), .out_width(5)) bit_extender_2 (.in(y_q), .out(bit_extender_2_out));
  Shifter #(.width(32), .shift("lr")) shifter_1 (.in(32'h80000000), .\dist (bit_extender_1_out), .out(shifter_1_out));
  assign xnor_1_out = ~(bit_extender_2_out ^ in_4);  // XNOR_Gate xnor_1, 5 bits wide
  and and_3 (and_3_out, xnor_1_out[0], xnor_1_out[1], xnor_1_out[2], xnor_1_out[3], xnor_1_out[4]);
  Transistor #(.\type ("n"), .width(32)) transistor_5 (.in(shifter_1_out), .out(out_5), .gate(and_3_out));
  Transistor #(.gate("br"), .width(32)) transistor_6 (.in({32{1'b0}}), .out(out_5), .gate(and_3_out));
endmodule

module _32_buffer_extendable__4 (
  input  [31:0] in_1,
  input  w,
  input  block,
  input  [4:0] y,
  output [31:0] out_5,
  output [31:0] out_6,
  output [31:0] out_7,
  output [31:0] out_8,
  output [31:0] out_9,
  output [31:0] out_10,
  output [31:0] out_11,
  output [31:0] out_12,
  output [31:0] out_13,
  output [31:0] out_14,
  output [31:0] out_15,
  output [31:0] out_16,
  output [31:0] out_17,
  output [31:0] out_18,
  output [31:0] out_19,
  output [31:0] out_20,
  output [31:0] out_21,
  output [31:0] out_22,
  output [31:0] out_23,
  output [31:0] out_24,
  output [31:0] out_25,
  output [31:0] out_26,
  output [31:0] out_27,
  output [31:0] out_28,
  output [31:0] out_29,
  output [31:0] out_30,
  output [31:0] out_31,
  output [31:0] out_32,
  output [31:0] out_33,
  output [31:0] out_34,
  output [31:0] out_35,
  output [31:0] out_36
);

  wire _0, _1, _2, _3, _4, _5, _6, _7, _8, _9, _10, _11, _12, _13, _14, _15, _16, _17, _18, _19, _20, _21,
       _22, _23, _24, _25, _26, _27, _28, _29, _30, _31, clock_1_out, nor_1_out;

  Demultiplexer #(.select(5), .disabled(0)) demultiplexer_1 (
    .out0(_0), .out1(_1), .out2(_2), .out3(_3), .out4(_4), .out5(_5), .out6(_6), .out7(_7), .out8(_8),
    .out9(_9), .out10(_10), .out11(_11), .out12(_12), .out13(_13), .out14(_14), .out15(_15), .out16(_16),
    .out17(_17), .out18(_18), .out19(_19), .out20(_20), .out21(_21), .out22(_22), .out23(_23), .out24(_24),
    .out25(_25), .out26(_26), .out27(_27), .out28(_28), .out29(_29), .out30(_30), .out31(_31), .in(1'b1),
    .sel(y), .en(nor_1_out));
  nor nor_1 (nor_1_out, block, clock_1_out);
  Clock clock_1 (.out(clock_1_out));
  _32buffer_el u_32buffer_el_1 (
    .\input (in_1), ._1___buffer_read(_0), .video(out_5), ._1___buffer_write___clr(w));  // open: out_5
  _32buffer_el u_32buffer_el_2 (
    .\input (in_1), ._1___buffer_read(_1), .video(out_6), ._1___buffer_write___clr(w));  // open: out_5
  _32buffer_el u_32buffer_el_3 (
    .\input (in_1), ._1___buffer_read(_2), .video(out_7), ._1___buffer_write___clr(w));  // open: out_5
  _32buffer_el u_32buffer_el_4 (
    .\input (in_1), ._1___buffer_read(_3), .video(out_8), ._1___buffer_write___clr(w));  // open: out_5
  _32buffer_el u_32buffer_el_5 (
    .\input (in_1), ._1___buffer_read(_4), .video(out_9), ._1___buffer_write___clr(w));  // open: out_5
  _32buffer_el u_32buffer_el_6 (
    .\input (in_1), ._1___buffer_read(_5), .video(out_10), ._1___buffer_write___clr(w));  // open: out_5
  _32buffer_el u_32buffer_el_7 (
    .\input (in_1), ._1___buffer_read(_6), .video(out_11), ._1___buffer_write___clr(w));  // open: out_5
  _32buffer_el u_32buffer_el_8 (
    .\input (in_1), ._1___buffer_read(_7), .video(out_12), ._1___buffer_write___clr(w));  // open: out_5
  _32buffer_el u_32buffer_el_9 (
    .\input (in_1), ._1___buffer_read(_8), .video(out_13), ._1___buffer_write___clr(w));  // open: out_5
  _32buffer_el u_32buffer_el_10 (
    .\input (in_1), ._1___buffer_read(_9), .video(out_14), ._1___buffer_write___clr(w));  // open: out_5
  _32buffer_el u_32buffer_el_11 (
    .\input (in_1), ._1___buffer_read(_10), .video(out_15), ._1___buffer_write___clr(w));  // open: out_5
  _32buffer_el u_32buffer_el_12 (
    .\input (in_1), ._1___buffer_read(_11), .video(out_16), ._1___buffer_write___clr(w));  // open: out_5
  _32buffer_el u_32buffer_el_13 (
    .\input (in_1), ._1___buffer_read(_12), .video(out_17), ._1___buffer_write___clr(w));  // open: out_5
  _32buffer_el u_32buffer_el_14 (
    .\input (in_1), ._1___buffer_read(_13), .video(out_18), ._1___buffer_write___clr(w));  // open: out_5
  _32buffer_el u_32buffer_el_15 (
    .\input (in_1), ._1___buffer_read(_14), .video(out_19), ._1___buffer_write___clr(w));  // open: out_5
  _32buffer_el u_32buffer_el_16 (
    .\input (in_1), ._1___buffer_read(_15), .video(out_20), ._1___buffer_write___clr(w));  // open: out_5
  _32buffer_el u_32buffer_el_17 (
    .\input (in_1), ._1___buffer_read(_16), .video(out_21), ._1___buffer_write___clr(w));  // open: out_5
  _32buffer_el u_32buffer_el_18 (
    .\input (in_1), ._1___buffer_read(_17), .video(out_22), ._1___buffer_write___clr(w));  // open: out_5
  _32buffer_el u_32buffer_el_19 (
    .\input (in_1), ._1___buffer_read(_18), .video(out_23), ._1___buffer_write___clr(w));  // open: out_5
  _32buffer_el u_32buffer_el_20 (
    .\input (in_1), ._1___buffer_read(_19), .video(out_24), ._1___buffer_write___clr(w));  // open: out_5
  _32buffer_el u_32buffer_el_21 (
    .\input (in_1), ._1___buffer_read(_20), .video(out_25), ._1___buffer_write___clr(w));  // open: out_5
  _32buffer_el u_32buffer_el_22 (
    .\input (in_1), ._1___buffer_read(_21), .video(out_26), ._1___buffer_write___clr(w));  // open: out_5
  _32buffer_el u_32buffer_el_23 (
    .\input (in_1), ._1___buffer_read(_22), .video(out_27), ._1___buffer_write___clr(w));  // open: out_5
  _32buffer_el u_32buffer_el_24 (
    .\input (in_1), ._1___buffer_read(_23), .video(out_28), ._1___buffer_write___clr(w));  // open: out_5
  _32buffer_el u_32buffer_el_25 (
    .\input (in_1), ._1___buffer_read(_24), .video(out_29), ._1___buffer_write___clr(w));  // open: out_5
  _32buffer_el u_32buffer_el_26 (
    .\input (in_1), ._1___buffer_read(_25), .video(out_30), ._1___buffer_write___clr(w));  // open: out_5
  _32buffer_el u_32buffer_el_27 (
    .\input (in_1), ._1___buffer_read(_26), .video(out_31), ._1___buffer_write___clr(w));  // open: out_5
  _32buffer_el u_32buffer_el_28 (
    .\input (in_1), ._1___buffer_read(_27), .video(out_32), ._1___buffer_write___clr(w));  // open: out_5
  _32buffer_el u_32buffer_el_29 (
    .\input (in_1), ._1___buffer_read(_28), .video(out_33), ._1___buffer_write___clr(w));  // open: out_5
  _32buffer_el u_32buffer_el_30 (
    .\input (in_1), ._1___buffer_read(_29), .video(out_34), ._1___buffer_write___clr(w));  // open: out_5
  _32buffer_el u_32buffer_el_31 (
    .\input (in_1), ._1___buffer_read(_30), .video(out_35), ._1___buffer_write___clr(w));  // open: out_5
  _32buffer_el u_32buffer_el_32 (
    .\input (in_1), ._1___buffer_read(_31), .video(out_36), ._1___buffer_write___clr(w));  // open: out_5

  // Other names for the same wires on the sheet: inp[31:0] = in_1

  // Notes on the sheet:
  //   block: pull=down
endmodule

module _64x64_ball (
  input  [6:0] vx,
  input  [6:0] vy,
  input  in_3,
  input  [5:0] cur_row,
  output [6:0] debug_x,
  output [6:0] debug_y,
  output [31:0] line_x1,
  output [31:0] line_x2
);

  wire and_1_out, and_2_out, and_3_out, and_4_out, and_5_out, clock_1_out, clock_2_out, counter_1_q,
       counter_2_q, nor_1_out, nor_2_out, not_1_out, not_2_out, or_1_out, or_2_out;
  wire [4:0] demultiplexer_1_out0, demultiplexer_1_out1;
  wire [5:0] bit_extender_1_out, bit_extender_2_out, xnor_1_out;
  wire [6:0] adder_1_out, adder_2_out, negator_1_out, negator_2_out, transistor_1_out, transistor_3_out,
       xv_q, yv_q;
  wire [31:0] shifter_1_out, shifter_2_out;

  // Probe on vx
  // Probe on vy
  Negator #(.width(7)) negator_1 (.in(vx), .out(negator_1_out));
  Transistor #(.\type ("n"), .gate("br"), .width(7)) transistor_1 (
    .in(negator_1_out), .out(transistor_1_out), .gate(counter_2_q));
  Transistor #(.width(7)) transistor_2 (.in(vx), .out(transistor_1_out), .gate(counter_2_q));
  Negator #(.width(7)) negator_2 (.in(vy), .out(negator_2_out));
  Transistor #(.\type ("n"), .gate("br"), .width(7)) transistor_3 (
    .in(negator_2_out), .out(transistor_3_out), .gate(counter_1_q));
  Transistor #(.width(7)) transistor_4 (.in(vy), .out(transistor_3_out), .gate(counter_1_q));
  Counter #(.width(1), .max('h1)) counter_1 (.Q(counter_1_q), .clk(or_1_out));  // open: load, D, count, carry, clr
  and and_1 (and_1_out, bit_extender_2_out[0], bit_extender_2_out[1], bit_extender_2_out[2], bit_extender_2_out[3], bit_extender_2_out[4], bit_extender_2_out[5]);
  or or_1 (or_1_out, and_1_out, nor_1_out);
  nor nor_1 (nor_1_out, bit_extender_2_out[0], bit_extender_2_out[1], bit_extender_2_out[2], bit_extender_2_out[3], bit_extender_2_out[4], bit_extender_2_out[5]);
  Counter #(.width(1), .max('h1)) counter_2 (.Q(counter_2_q), .clk(or_2_out));  // open: load, D, count, carry, clr
  and and_2 (and_2_out, bit_extender_1_out[0], bit_extender_1_out[1], bit_extender_1_out[2], bit_extender_1_out[3], bit_extender_1_out[4], bit_extender_1_out[5]);
  or or_2 (or_2_out, and_2_out, nor_2_out);
  nor nor_2 (nor_2_out, bit_extender_1_out[0], bit_extender_1_out[1], bit_extender_1_out[2], bit_extender_1_out[3], bit_extender_1_out[4], bit_extender_1_out[5]);
  Register #(.width(7)) xv (.D(transistor_1_out), .Q(xv_q), .clk(clock_1_out));  // open: en, clr
  Clock clock_1 (.out(clock_1_out));
  Register #(.width(7)) yv (.D(transistor_3_out), .Q(yv_q), .clk(clock_2_out));  // open: en, clr
  Clock clock_2 (.out(clock_2_out));
  Adder #(.width(7)) adder_1 (.a(xv_q), .b(debug_x), .out(adder_1_out));  // open: cin, cout
  Adder #(.width(7)) adder_2 (.a(yv_q), .b(debug_y), .out(adder_2_out));  // open: cin, cout
  Register #(.width(7)) x (.D(adder_1_out), .Q(debug_x), .clk(in_3));  // open: en, clr
  Register #(.width(7)) y (.D(adder_2_out), .Q(debug_y), .clk(in_3));  // open: en, clr
  // Probe on cur_row
  Demultiplexer #(.width(5), .enable("false")) demultiplexer_1 (
    .out0(demultiplexer_1_out0), .out1(demultiplexer_1_out1), .in(bit_extender_1_out[4:0]), .sel(not_1_out));
  not not_1 (not_1_out, bit_extender_1_out[5]);
  Bit_Extender #(.in_width(7), .out_width(6)) bit_extender_1 (.in(debug_x), .out(bit_extender_1_out));
  // Probe on bit_extender_2_out
  Bit_Extender #(.in_width(7), .out_width(6)) bit_extender_2 (.in(debug_y), .out(bit_extender_2_out));
  assign xnor_1_out = ~(bit_extender_2_out ^ cur_row);  // XNOR_Gate xnor_1, 6 bits wide
  Shifter #(.width(32), .shift("lr")) shifter_1 (.in(32'h80000000), .\dist (demultiplexer_1_out1), .out(shifter_1_out));
  not not_2 (not_2_out, bit_extender_1_out[5]);
  and and_3 (and_3_out, xnor_1_out[0], xnor_1_out[1], xnor_1_out[2], xnor_1_out[3], xnor_1_out[4], xnor_1_out[5]);
  and and_4 (and_4_out, and_3_out, not_2_out);
  Transistor #(.gate("br"), .width(32)) transistor_5 (.in({32{1'b0}}), .out(line_x1), .gate(and_4_out));
  Transistor #(.\type ("n"), .width(32)) transistor_6 (.in(shifter_1_out), .out(line_x1), .gate(and_4_out));
  and and_5 (and_5_out, bit_extender_1_out[5], and_3_out);
  Shifter #(.width(32), .shift("lr")) shifter_2 (.in(32'h80000000), .\dist (demultiplexer_1_out0), .out(shifter_2_out));
  Transistor #(.gate("br"), .width(32)) transistor_7 (.in({32{1'b0}}), .out(line_x2), .gate(and_5_out));
  Transistor #(.\type ("n"), .width(32)) transistor_8 (.in(shifter_2_out), .out(line_x2), .gate(and_5_out));
endmodule

module obj_module (
  input  [6:0] vx,
  input  [6:0] vy,
  input  update,
  input  [5:0] cur_line,
  output [31:0] line_x1,
  output [31:0] line_x2
);

  wire and_1_out, and_2_out, and_3_out, clock_1_out, clock_2_out, comparator_1_eq, comparator_1_gt,
       comparator_2_lt, comparator_3_lt, comparator_4_eq, comparator_4_gt, comparator_5_lt, comparator_6_eq,
       counter_1_q, counter_2_q, not_1_out, not_2_out, not_3_out, or_1_out, or_2_out, or_3_out, or_4_out,
       subtractor_2_bout, subtractor_3_bout;
  wire [4:0] bit_extender_3_out, bit_extender_4_out, multiplexer_1_out, multiplexer_2_out, multiplexer_4_out,
       subtractor_3_out, subtractor_4_out;
  wire [5:0] bit_extender_1_out, bit_extender_2_out, subtractor_1_out, subtractor_2_out;
  wire [6:0] adder_1_out, adder_2_out, negator_1_out, negator_2_out, transistor_1_out, transistor_3_out, x_q,
       xv_q, y_q, yv_q;
  wire [31:0] n32_bit_reverse_1_out_2, rom_1_data, shifter_1_out, shifter_2_out, shifter_3_out;

  // Probe on vx
  // Probe on vy
  Counter #(.width(1), .max('h1)) counter_1 (.Q(counter_1_q), .clk(or_1_out));  // open: load, D, count, carry, clr
  or or_1 (or_1_out, comparator_3_lt, or_3_out);
  Negator #(.width(7)) negator_1 (.in(vx), .out(negator_1_out));
  Transistor #(.\type ("n"), .gate("br"), .width(7)) transistor_1 (
    .in(negator_1_out), .out(transistor_1_out), .gate(counter_1_q));
  Transistor #(.width(7)) transistor_2 (.in(vx), .out(transistor_1_out), .gate(counter_1_q));
  Negator #(.width(7)) negator_2 (.in(vy), .out(negator_2_out));
  Counter #(.width(1), .max('h1)) counter_2 (.Q(counter_2_q), .clk(or_2_out));  // open: load, D, count, carry, clr
  or or_2 (or_2_out, or_4_out, comparator_2_lt);
  Register #(.width(7)) xv (.D(transistor_1_out), .Q(xv_q), .clk(clock_1_out));  // open: en, clr
  Clock clock_1 (.out(clock_1_out));
  Transistor #(.\type ("n"), .gate("br"), .width(7)) transistor_3 (
    .in(negator_2_out), .out(transistor_3_out), .gate(counter_2_q));
  Transistor #(.width(7)) transistor_4 (.in(vy), .out(transistor_3_out), .gate(counter_2_q));
  Register #(.width(7)) yv (.D(transistor_3_out), .Q(yv_q), .clk(clock_2_out));  // open: en, clr
  Clock clock_2 (.out(clock_2_out));
  Comparator #(.width(7)) comparator_1 (
    .a({7{1'b0}}), .b(y_q), .gt(comparator_1_gt), .eq(comparator_1_eq));  // open: lt
  Comparator #(.width(7)) comparator_2 (.a(7'b0111100), .b(y_q), .lt(comparator_2_lt));  // open: gt, eq
  Comparator #(.width(7)) comparator_3 (.a(7'b0111100), .b(x_q), .lt(comparator_3_lt));  // open: gt, eq
  or or_3 (or_3_out, comparator_4_gt, comparator_4_eq);
  Comparator #(.width(7)) comparator_4 (
    .a({7{1'b0}}), .b(x_q), .gt(comparator_4_gt), .eq(comparator_4_eq));  // open: lt
  Adder #(.width(7)) adder_1 (.a(xv_q), .b(x_q), .out(adder_1_out));  // open: cin, cout
  Adder #(.width(7)) adder_2 (.a(yv_q), .b(y_q), .out(adder_2_out));  // open: cin, cout
  or or_4 (or_4_out, comparator_1_gt, comparator_1_eq);
  Register #(.width(7)) x (.D(adder_1_out), .Q(x_q), .clk(update));  // open: en, clr
  Register #(.width(7)) y (.D(adder_2_out), .Q(y_q), .clk(update));  // open: en, clr
  Bit_Extender #(.in_width(7), .out_width(6)) bit_extender_1 (.in(x_q), .out(bit_extender_1_out));
  Bit_Extender #(.in_width(7), .out_width(6)) bit_extender_2 (.in(y_q), .out(bit_extender_2_out));
  Subtractor #(.width(6)) subtractor_1 (
    .a(cur_line), .b(bit_extender_2_out), .out(subtractor_1_out));  // open: bin, bout
  Subtractor #(.width(6)) subtractor_2 (
    .a(cur_line), .b(bit_extender_2_out), .out(subtractor_2_out), .bout(subtractor_2_bout));  // open: bin
  // Probe on cur_line
  Bit_Extender #(.in_width(6), .out_width(5)) bit_extender_3 (.in(subtractor_1_out), .out(bit_extender_3_out));
  Comparator #(.width(6), .mode("unsigned")) comparator_5 (
    .a(subtractor_2_out), .b(6'b100000), .lt(comparator_5_lt));  // open: gt, eq
  // Probe on bit_extender_1_out[4:0]
  not not_1 (not_1_out, bit_extender_1_out[5]);
  not not_2 (not_2_out, comparator_6_eq);
  Comparator #(.width(6), .mode("unsigned")) comparator_6 (
    .a(bit_extender_1_out), .b({6{1'b0}}), .eq(comparator_6_eq));  // open: gt, lt
  and and_1 (and_1_out, comparator_5_lt, not_3_out);
  not not_3 (not_3_out, subtractor_2_bout);
  ROM #(.addrWidth(5), .dataWidth(32)) rom_1 (.addr(bit_extender_3_out), .data(rom_1_data));  // open: sel
  assign bit_extender_4_out = {{4{1'b0}}, not_1_out};  // Bit_Extender bit_extender_4
  _32_bit_reverse u_32_bit_reverse_1 (.in_1(rom_1_data), .out_2(n32_bit_reverse_1_out_2));
  Subtractor #(.width(5)) subtractor_3 (
    .a(bit_extender_1_out[4:0]), .b(bit_extender_4_out), .out(subtractor_3_out), .bout(subtractor_3_bout));  // open: bin
  Multiplexer #(.width(5), .enable("false")) multiplexer_1 (
    .in0(subtractor_3_out), .in1({5{1'b0}}), .out(multiplexer_1_out), .sel(subtractor_3_bout));
  // Probe on {5{1'b1}}
  // Probe on subtractor_4_out
  Subtractor #(.width(5)) subtractor_4 (
    .a({5{1'b1}}), .b(multiplexer_1_out), .out(subtractor_4_out));  // open: bin, bout
  Shifter #(.width(32), .shift("lr")) shifter_1 (
    .in(n32_bit_reverse_1_out_2), .\dist (bit_extender_1_out[4:0]), .out(shifter_1_out));
  and and_2 (and_2_out, not_1_out, and_1_out);
  Multiplexer #(.width(5), .enable("false")) multiplexer_2 (
    .in0({5{1'b0}}), .in1(subtractor_4_out), .out(multiplexer_2_out), .sel(not_1_out));
  Multiplexer #(.width(32), .enable("false")) multiplexer_3 (
    .in0({32{1'b0}}), .in1(shifter_1_out), .out(line_x1), .sel(and_2_out));
  Shifter #(.width(32)) shifter_2 (.in(n32_bit_reverse_1_out_2), .\dist (multiplexer_2_out), .out(shifter_2_out));
  Multiplexer #(.width(5), .enable("false")) multiplexer_4 (
    .in0(bit_extender_1_out[4:0]), .in1({5{1'b0}}), .out(multiplexer_4_out), .sel(not_1_out));
  Shifter #(.width(32), .shift("lr")) shifter_3 (.in(shifter_2_out), .\dist (multiplexer_4_out), .out(shifter_3_out));
  and and_3 (and_3_out, not_2_out, and_1_out);
  Multiplexer #(.width(32), .enable("false")) multiplexer_5 (
    .in0({32{1'b0}}), .in1(shifter_3_out), .out(line_x2), .sel(and_3_out));

  // Notes on the sheet:
  //   address = y-line
  //   0 <= y-line < 32
  //   contents of rom_1 (hex, n*v repeats v):
  //   5 2 5
  //   +1 for shift left line x2
  //   to simulate shift by 32
  //   idk i just like that
  //   smth will work on line x2
  //   only if shift right > 0
  //   (still for simulate 32 shift)
  //   line x1 will work only if shift right < 32
  //   if x=0 shift left for line x2 must be 32 (with simulation of 32 shift)
  //   shift left for line x2
  //   shift rigth for line x2
  //   shift right works only if shift left = 0
endmodule

module _32_bit_reverse (
  input  [31:0] in_1,
  output [31:0] out_2
);


  assign out_2 = {in_1[0], in_1[1], in_1[2], in_1[3], in_1[4], in_1[5], in_1[6], in_1[7], in_1[8], in_1[9], in_1[10], in_1[11], in_1[12], in_1[13], in_1[14], in_1[15], in_1[16], in_1[17], in_1[18], in_1[19], in_1[20], in_1[21], in_1[22], in_1[23], in_1[24], in_1[25], in_1[26], in_1[27], in_1[28], in_1[29], in_1[30], in_1[31]};
endmodule

module abst_obj (
  input  write,
  input  [4:0] texture_line,
  input  [31:0] texture_input,
  input  [6:0] x,
  input  [6:0] y,
  input  draw,
  output [31:0] line_x1,
  output [31:0] line_x2,
  output [5:0] cur_line,
  output drawing
);

  wire and_1_out, and_2_out, and_3_out, comparator_1_lt, comparator_2_eq, counter_1_carry, drawing_q,
       not_1_out, not_2_out, not_4_out, not_5_out, not_6_out, register_1_q, subtractor_2_bout,
       subtractor_3_bout, transistor_3_out, x_upt, y_upd;
  wire [4:0] bit_extender_3_out, bit_extender_5_out, counter_1_q, multiplexer_1_out, multiplexer_2_out,
       multiplexer_4_out, subtractor_3_out, subtractor_4_out, transistor_1_out;
  wire [5:0] adder_1_out, bit_extender_1_out, bit_extender_2_out, bit_extender_4_out, subtractor_1_out,
       subtractor_2_out;
  wire [31:0] n32_bit_reverse_1_out_2, ram_1_data, shifter_1_out, shifter_2_out, shifter_3_out;

  // Probe on x
  // Probe on y
  Register #(.width(1)) register_1 (.D(draw), .Q(register_1_q), .clk(draw), .clr(counter_1_carry));  // open: en
  Register #(.width(1)) u_drawing (
    .D(register_1_q), .Q(drawing_q), .clk(not_1_out), .clr(counter_1_carry));  // open: en
  not not_1 (not_1_out, y_upd);
  or or_1 (drawing, register_1_q, drawing_q);
  Bit_Extender #(.in_width(7), .out_width(6)) bit_extender_1 (.in(x), .out(bit_extender_1_out));
  Bit_Extender #(.in_width(7), .out_width(6)) bit_extender_2 (.in(y), .out(bit_extender_2_out));
  // Probe on adder_1_out
  Subtractor #(.width(6)) subtractor_1 (
    .a(adder_1_out), .b(bit_extender_2_out), .out(subtractor_1_out));  // open: bin, bout
  Bit_Extender #(.in_width(6), .out_width(5)) bit_extender_3 (.in(subtractor_1_out), .out(bit_extender_3_out));
  Counter #(.width(5), .max('h3)) counter_1 (
    .count(drawing_q), .Q(counter_1_q), .carry(counter_1_carry), .clk(x_upt), .clr(counter_1_carry));  // open: load, D
  Subtractor #(.width(6)) subtractor_2 (
    .a(adder_1_out), .b(bit_extender_2_out), .out(subtractor_2_out), .bout(subtractor_2_bout));  // open: bin
  not not_2 (not_2_out, drawing_q);
  Register #(.width(6)) register_2 (.D(adder_1_out), .Q(cur_line), .clk(y_upd), .clr(not_2_out));  // open: en
  Transistor #(.gate("br"), .width(5)) transistor_1 (.in(texture_line), .out(transistor_1_out), .gate(register_1_q));
  Transistor #(.\type ("n"), .width(5)) transistor_2 (
    .in(bit_extender_3_out), .out(transistor_1_out), .gate(register_1_q));
  assign bit_extender_4_out = {{1{1'b0}}, counter_1_q};  // Bit_Extender bit_extender_4
  Comparator #(.width(6), .mode("unsigned")) comparator_1 (
    .a(subtractor_2_out), .b(6'b100000), .lt(comparator_1_lt));  // open: gt, eq
  not not_3 (x_upt, y_upd);
  Transistor #(.gate("br")) transistor_3 (.in(write), .out(transistor_3_out), .gate(register_1_q));
  // Probe on bit_extender_1_out[4:0]
  not not_4 (not_4_out, bit_extender_1_out[5]);
  Adder #(.width(6)) adder_1 (.a(bit_extender_2_out), .b(bit_extender_4_out), .out(adder_1_out));  // open: cin, cout
  not not_5 (not_5_out, comparator_2_eq);
  Comparator #(.width(6), .mode("unsigned")) comparator_2 (
    .a(bit_extender_1_out), .b({6{1'b0}}), .eq(comparator_2_eq));  // open: gt, lt
  and and_1 (and_1_out, comparator_1_lt, not_6_out);
  not not_6 (not_6_out, subtractor_2_bout);
  Clock clock_1 (.out(y_upd));
  assign bit_extender_5_out = {{4{1'b0}}, not_4_out};  // Bit_Extender bit_extender_5
  RAM #(.addrWidth(5), .dataWidth(32), .bus("separate")) ram_1 (
    .addr(transistor_1_out), .din(texture_input), .data(ram_1_data), .clk(transistor_3_out));  // open: str, sel, ld, clr
  _32_bit_reverse u_32_bit_reverse_1 (.in_1(ram_1_data), .out_2(n32_bit_reverse_1_out_2));
  Subtractor #(.width(5)) subtractor_3 (
    .a(bit_extender_1_out[4:0]), .b(bit_extender_5_out), .out(subtractor_3_out), .bout(subtractor_3_bout));  // open: bin
  Multiplexer #(.width(5), .enable("false")) multiplexer_1 (
    .in0(subtractor_3_out), .in1({5{1'b0}}), .out(multiplexer_1_out), .sel(subtractor_3_bout));
  // Probe on {5{1'b1}}
  // Probe on subtractor_4_out
  Subtractor #(.width(5)) subtractor_4 (
    .a({5{1'b1}}), .b(multiplexer_1_out), .out(subtractor_4_out));  // open: bin, bout
  Shifter #(.width(32), .shift("lr")) shifter_1 (
    .in(n32_bit_reverse_1_out_2), .\dist (bit_extender_1_out[4:0]), .out(shifter_1_out));
  Multiplexer #(.width(5), .enable("false")) multiplexer_2 (
    .in0({5{1'b0}}), .in1(subtractor_4_out), .out(multiplexer_2_out), .sel(not_4_out));
  and and_2 (and_2_out, not_4_out, register_1_q, drawing_q, and_1_out);
  Multiplexer #(.width(32), .enable("false")) multiplexer_3 (
    .in0({32{1'b0}}), .in1(shifter_1_out), .out(line_x1), .sel(and_2_out));
  Shifter #(.width(32)) shifter_2 (.in(n32_bit_reverse_1_out_2), .\dist (multiplexer_2_out), .out(shifter_2_out));
  Multiplexer #(.width(5), .enable("false")) multiplexer_4 (
    .in0(bit_extender_1_out[4:0]), .in1({5{1'b0}}), .out(multiplexer_4_out), .sel(not_4_out));
  Shifter #(.width(32), .shift("lr")) shifter_3 (.in(shifter_2_out), .\dist (multiplexer_4_out), .out(shifter_3_out));
  and and_3 (and_3_out, not_5_out, register_1_q, and_1_out, drawing_q);
  Multiplexer #(.width(32), .enable("false")) multiplexer_5 (
    .in0({32{1'b0}}), .in1(shifter_3_out), .out(line_x2), .sel(and_3_out));

  // Notes on the sheet:
  //   address = line-y
  //   0 <= y-line < 32
  //   +1 for shift left line x2
  //   to simulate shift by 32
  //   idk i just like that
  //   line x1 will work only if shift right < 32
  //   smth will work on line x2
  //   only if shift right > 0
  //   (still for simulate 32 shift)
  //   if x=0 shift left for line x2 must be 32 (with simulation of 32 shift)
  //   shift left for line x2
  //   shift rigth for line x2
  //   shift right works only if shift left = 0
endmodule

module enemy_test (
  input  [15:0] in_1,
  input  [15:0] in_2,
  input  in_3
);

  wire abst_obj_1_drawing, clock_1_out, clock_2_out, comparator_1_eq, comparator_2_eq, counter_1_carry,
       counter_2_q, enemies_1_ready, not_1_out, not_2_out, not_3_out, not_4_out, pull_resistor_1_node,
       register_1_q, register_2_q, transistor_2_out, \wait , xor_1_out;
  wire [4:0] counter_1_q;
  wire [5:0] abst_obj_1_cur_line;
  wire [6:0] x, y;
  wire [15:0] adder_1_out, bit_extender_1_out, command, enemies_1_command, id, multiplexer_1_out,
       multiplier_1_out, register_4_q, subtractor_1_out, Xin, Yin;
  wire [31:0] abst_obj_1_line_x1, abst_obj_1_line_x2, n32video_buffer_extendable_1_out_5,
       n32video_buffer_extendable_1_out_6, n32video_buffer_extendable_1_out_7,
       n32video_buffer_extendable_1_out_8, n32video_buffer_extendable_1_out_9,
       n32video_buffer_extendable_1_out_10, n32video_buffer_extendable_1_out_11,
       n32video_buffer_extendable_1_out_12, n32video_buffer_extendable_1_out_13,
       n32video_buffer_extendable_1_out_14, n32video_buffer_extendable_1_out_15,
       n32video_buffer_extendable_1_out_16, n32video_buffer_extendable_1_out_17,
       n32video_buffer_extendable_1_out_18, n32video_buffer_extendable_1_out_19,
       n32video_buffer_extendable_1_out_20, n32video_buffer_extendable_1_out_21,
       n32video_buffer_extendable_1_out_22, n32video_buffer_extendable_1_out_23,
       n32video_buffer_extendable_1_out_24, n32video_buffer_extendable_1_out_25,
       n32video_buffer_extendable_1_out_26, n32video_buffer_extendable_1_out_27,
       n32video_buffer_extendable_1_out_28, n32video_buffer_extendable_1_out_29,
       n32video_buffer_extendable_1_out_30, n32video_buffer_extendable_1_out_31,
       n32video_buffer_extendable_1_out_32, n32video_buffer_extendable_1_out_33,
       n32video_buffer_extendable_1_out_34, n32video_buffer_extendable_1_out_35,
       n32video_buffer_extendable_1_out_36, n32video_buffer_extendable_2_out_5,
       n32video_buffer_extendable_2_out_6, n32video_buffer_extendable_2_out_7,
       n32video_buffer_extendable_2_out_8, n32video_buffer_extendable_2_out_9,
       n32video_buffer_extendable_2_out_10, n32video_buffer_extendable_2_out_11,
       n32video_buffer_extendable_2_out_12, n32video_buffer_extendable_2_out_13,
       n32video_buffer_extendable_2_out_14, n32video_buffer_extendable_2_out_15,
       n32video_buffer_extendable_2_out_16, n32video_buffer_extendable_2_out_17,
       n32video_buffer_extendable_2_out_18, n32video_buffer_extendable_2_out_19,
       n32video_buffer_extendable_2_out_20, n32video_buffer_extendable_2_out_21,
       n32video_buffer_extendable_2_out_22, n32video_buffer_extendable_2_out_23,
       n32video_buffer_extendable_2_out_24, n32video_buffer_extendable_2_out_25,
       n32video_buffer_extendable_2_out_26, n32video_buffer_extendable_2_out_27,
       n32video_buffer_extendable_2_out_28, n32video_buffer_extendable_2_out_29,
       n32video_buffer_extendable_2_out_30, n32video_buffer_extendable_2_out_31,
       n32video_buffer_extendable_2_out_32, n32video_buffer_extendable_2_out_33,
       n32video_buffer_extendable_2_out_34, n32video_buffer_extendable_2_out_35,
       n32video_buffer_extendable_2_out_36, n32video_buffer_extendable_3_out_5,
       n32video_buffer_extendable_3_out_6, n32video_buffer_extendable_3_out_7,
       n32video_buffer_extendable_3_out_8, n32video_buffer_extendable_3_out_9,
       n32video_buffer_extendable_3_out_10, n32video_buffer_extendable_3_out_11,
       n32video_buffer_extendable_3_out_12, n32video_buffer_extendable_3_out_13,
       n32video_buffer_extendable_3_out_14, n32video_buffer_extendable_3_out_15,
       n32video_buffer_extendable_3_out_16, n32video_buffer_extendable_3_out_17,
       n32video_buffer_extendable_3_out_18, n32video_buffer_extendable_3_out_19,
       n32video_buffer_extendable_3_out_20, n32video_buffer_extendable_3_out_21,
       n32video_buffer_extendable_3_out_22, n32video_buffer_extendable_3_out_23,
       n32video_buffer_extendable_3_out_24, n32video_buffer_extendable_3_out_25,
       n32video_buffer_extendable_3_out_26, n32video_buffer_extendable_3_out_27,
       n32video_buffer_extendable_3_out_28, n32video_buffer_extendable_3_out_29,
       n32video_buffer_extendable_3_out_30, n32video_buffer_extendable_3_out_31,
       n32video_buffer_extendable_3_out_32, n32video_buffer_extendable_3_out_33,
       n32video_buffer_extendable_3_out_34, n32video_buffer_extendable_3_out_35,
       n32video_buffer_extendable_3_out_36, n32video_buffer_extendable_4_out_5,
       n32video_buffer_extendable_4_out_6, n32video_buffer_extendable_4_out_7,
       n32video_buffer_extendable_4_out_8, n32video_buffer_extendable_4_out_9,
       n32video_buffer_extendable_4_out_10, n32video_buffer_extendable_4_out_11,
       n32video_buffer_extendable_4_out_12, n32video_buffer_extendable_4_out_13,
       n32video_buffer_extendable_4_out_14, n32video_buffer_extendable_4_out_15,
       n32video_buffer_extendable_4_out_16, n32video_buffer_extendable_4_out_17,
       n32video_buffer_extendable_4_out_18, n32video_buffer_extendable_4_out_19,
       n32video_buffer_extendable_4_out_20, n32video_buffer_extendable_4_out_21,
       n32video_buffer_extendable_4_out_22, n32video_buffer_extendable_4_out_23,
       n32video_buffer_extendable_4_out_24, n32video_buffer_extendable_4_out_25,
       n32video_buffer_extendable_4_out_26, n32video_buffer_extendable_4_out_27,
       n32video_buffer_extendable_4_out_28, n32video_buffer_extendable_4_out_29,
       n32video_buffer_extendable_4_out_30, n32video_buffer_extendable_4_out_31,
       n32video_buffer_extendable_4_out_32, n32video_buffer_extendable_4_out_33,
       n32video_buffer_extendable_4_out_34, n32video_buffer_extendable_4_out_35,
       n32video_buffer_extendable_4_out_36, rom_1_data;

  abst_obj abst_obj_1 (
    .y(y), .texture_line(counter_1_q), .write(xor_1_out), .texture_input(rom_1_data), .draw(counter_1_carry),
    .cur_line(abst_obj_1_cur_line), .line_x1(abst_obj_1_line_x1), .line_x2(abst_obj_1_line_x2), .x(x),
    .drawing(abst_obj_1_drawing));
  Counter #(.width(5), .max('h3)) counter_1 (
    .Q(counter_1_q), .carry(counter_1_carry), .clk(pull_resistor_1_node), .clr(counter_1_carry));  // open: load, D, count
  Pull_Resistor pull_resistor_1 (.node(pull_resistor_1_node));
  Transistor #(.\type ("n"), .gate("br")) transistor_1 (
    .in(clock_1_out), .out(pull_resistor_1_node), .gate(register_2_q));
  Clock clock_1 (.out(clock_1_out));
  xor xor_1 (xor_1_out, pull_resistor_1_node, register_2_q);
  Counter #(.width(1), .max('h1)) counter_2 (
    .Q(counter_2_q), .clk(comparator_1_eq), .clr(abst_obj_1_drawing));  // open: load, D, count, carry
  Multiplexer #(.width(16), .enable("false")) multiplexer_1 (
    .in0(in_2), .in1(subtractor_1_out), .out(multiplexer_1_out), .sel(register_1_q));
  Register #(.width(1)) register_1 (.D(transistor_2_out), .Q(register_1_q), .clk(transistor_2_out));  // open: en, clr
  Register #(.width(1)) register_2 (
    .D(counter_2_q), .Q(register_2_q), .clk(not_1_out), .clr(abst_obj_1_drawing));  // open: en
  not not_1 (not_1_out, clock_2_out);
  Clock clock_2 (.out(clock_2_out));
  Register #(.width(16)) register_3 (.D(in_1), .clk(transistor_2_out));  // open: en, Q, clr
  Register #(.width(16)) register_4 (.D(multiplexer_1_out), .Q(register_4_q), .clk(transistor_2_out));  // open: en, clr
  Transistor transistor_2 (.in(in_3), .out(transistor_2_out), .gate(\wait ));
  // Probe on id
  or or_1 (\wait , register_2_q, counter_2_q, abst_obj_1_drawing);
  Subtractor #(.width(16)) subtractor_1 (.a(register_4_q), .b(16'h1), .out(subtractor_1_out));  // open: bin, bout
  assign bit_extender_1_out = {{11{1'b0}}, counter_1_q};  // Bit_Extender bit_extender_1
  Bit_Extender #(.in_width(16), .out_width(7)) bit_extender_2 (.in(Xin), .out(x));
  Bit_Extender #(.in_width(16), .out_width(7)) bit_extender_3 (.in(Yin), .out(y));
  // Probe on command
  // Probe on abst_obj_1_cur_line
  Multiplier #(.width(16)) multiplier_1 (.a(id), .b(16'h3), .out(multiplier_1_out));  // open: cin, cout
  Comparator #(.width(16), .mode("unsigned")) comparator_1 (
    .a(command), .b(16'h1), .eq(comparator_1_eq));  // open: gt, lt
  Comparator #(.width(16), .mode("unsigned")) comparator_2 (
    .a(command), .b(16'h2), .eq(comparator_2_eq));  // open: gt, lt
  enemies enemies_1 (
    .\wait (\wait ), .draw(enemies_1_ready), .id(id), .y(Xin), .x(Yin), .command(enemies_1_command),
    .ready(enemies_1_ready));  // open: initing, collide, clock, DEBUG__enemy_cout
  Adder #(.width(16)) adder_1 (.a(bit_extender_1_out), .b(multiplier_1_out), .out(adder_1_out));  // open: cin, cout
  // Probe on x
  // Probe on y
  // Probe on abst_obj_1_line_x1
  not not_2 (not_2_out, abst_obj_1_cur_line[5]);
  Multiplexer #(.width(16), .enable("false")) multiplexer_2 (
    .in0(enemies_1_command), .in1(16'h2), .out(command), .sel(enemies_1_ready));
  ROM #(.addrWidth(16), .dataWidth(32)) rom_1 (.addr(adder_1_out), .data(rom_1_data));  // open: sel
  // Probe on abst_obj_1_line_x2
  not not_3 (not_3_out, not_2_out);
  _32video_buffer_extendable u_32video_buffer_extendable_1 (
    .in_1(abst_obj_1_line_x1), .out_5(n32video_buffer_extendable_1_out_5),
    .out_6(n32video_buffer_extendable_1_out_6), .out_7(n32video_buffer_extendable_1_out_7),
    .out_8(n32video_buffer_extendable_1_out_8), .out_9(n32video_buffer_extendable_1_out_9),
    .out_10(n32video_buffer_extendable_1_out_10), .out_11(n32video_buffer_extendable_1_out_11),
    .out_12(n32video_buffer_extendable_1_out_12), .out_13(n32video_buffer_extendable_1_out_13),
    .out_14(n32video_buffer_extendable_1_out_14), .out_15(n32video_buffer_extendable_1_out_15),
    .out_16(n32video_buffer_extendable_1_out_16), .out_17(n32video_buffer_extendable_1_out_17),
    .out_18(n32video_buffer_extendable_1_out_18), .out_19(n32video_buffer_extendable_1_out_19),
    .out_20(n32video_buffer_extendable_1_out_20), .out_21(n32video_buffer_extendable_1_out_21),
    .out_22(n32video_buffer_extendable_1_out_22), .out_23(n32video_buffer_extendable_1_out_23),
    .out_24(n32video_buffer_extendable_1_out_24), .out_25(n32video_buffer_extendable_1_out_25),
    .out_26(n32video_buffer_extendable_1_out_26), .out_27(n32video_buffer_extendable_1_out_27),
    .out_28(n32video_buffer_extendable_1_out_28), .out_29(n32video_buffer_extendable_1_out_29),
    .out_30(n32video_buffer_extendable_1_out_30), .out_31(n32video_buffer_extendable_1_out_31),
    .out_32(n32video_buffer_extendable_1_out_32), .out_33(n32video_buffer_extendable_1_out_33),
    .out_34(n32video_buffer_extendable_1_out_34), .out_35(n32video_buffer_extendable_1_out_35),
    .out_36(n32video_buffer_extendable_1_out_36), .block(not_3_out), .y(abst_obj_1_cur_line[4:0]),
    .w(comparator_2_eq));
  DotMatrix #(.inputtype("row"), .matrixcols(32), .matrixrows(32)) dotmatrix_1 (
    .row0(n32video_buffer_extendable_1_out_5), .row1(n32video_buffer_extendable_1_out_6),
    .row2(n32video_buffer_extendable_1_out_7), .row3(n32video_buffer_extendable_1_out_8),
    .row4(n32video_buffer_extendable_1_out_9), .row5(n32video_buffer_extendable_1_out_10),
    .row6(n32video_buffer_extendable_1_out_11), .row7(n32video_buffer_extendable_1_out_12),
    .row8(n32video_buffer_extendable_1_out_13), .row9(n32video_buffer_extendable_1_out_14),
    .row10(n32video_buffer_extendable_1_out_15), .row11(n32video_buffer_extendable_1_out_16),
    .row12(n32video_buffer_extendable_1_out_17), .row13(n32video_buffer_extendable_1_out_18),
    .row14(n32video_buffer_extendable_1_out_19), .row15(n32video_buffer_extendable_1_out_20),
    .row16(n32video_buffer_extendable_1_out_21), .row17(n32video_buffer_extendable_1_out_22),
    .row18(n32video_buffer_extendable_1_out_23), .row19(n32video_buffer_extendable_1_out_24),
    .row20(n32video_buffer_extendable_1_out_25), .row21(n32video_buffer_extendable_1_out_26),
    .row22(n32video_buffer_extendable_1_out_27), .row23(n32video_buffer_extendable_1_out_28),
    .row24(n32video_buffer_extendable_1_out_29), .row25(n32video_buffer_extendable_1_out_30),
    .row26(n32video_buffer_extendable_1_out_31), .row27(n32video_buffer_extendable_1_out_32),
    .row28(n32video_buffer_extendable_1_out_33), .row29(n32video_buffer_extendable_1_out_34),
    .row30(n32video_buffer_extendable_1_out_35), .row31(n32video_buffer_extendable_1_out_36));
  DotMatrix #(.inputtype("row"), .matrixcols(32), .matrixrows(32)) dotmatrix_2 (
    .row0(n32video_buffer_extendable_2_out_5), .row1(n32video_buffer_extendable_2_out_6),
    .row2(n32video_buffer_extendable_2_out_7), .row3(n32video_buffer_extendable_2_out_8),
    .row4(n32video_buffer_extendable_2_out_9), .row5(n32video_buffer_extendable_2_out_10),
    .row6(n32video_buffer_extendable_2_out_11), .row7(n32video_buffer_extendable_2_out_12),
    .row8(n32video_buffer_extendable_2_out_13), .row9(n32video_buffer_extendable_2_out_14),
    .row10(n32video_buffer_extendable_2_out_15), .row11(n32video_buffer_extendable_2_out_16),
    .row12(n32video_buffer_extendable_2_out_17), .row13(n32video_buffer_extendable_2_out_18),
    .row14(n32video_buffer_extendable_2_out_19), .row15(n32video_buffer_extendable_2_out_20),
    .row16(n32video_buffer_extendable_2_out_21), .row17(n32video_buffer_extendable_2_out_22),
    .row18(n32video_buffer_extendable_2_out_23), .row19(n32video_buffer_extendable_2_out_24),
    .row20(n32video_buffer_extendable_2_out_25), .row21(n32video_buffer_extendable_2_out_26),
    .row22(n32video_buffer_extendable_2_out_27), .row23(n32video_buffer_extendable_2_out_28),
    .row24(n32video_buffer_extendable_2_out_29), .row25(n32video_buffer_extendable_2_out_30),
    .row26(n32video_buffer_extendable_2_out_31), .row27(n32video_buffer_extendable_2_out_32),
    .row28(n32video_buffer_extendable_2_out_33), .row29(n32video_buffer_extendable_2_out_34),
    .row30(n32video_buffer_extendable_2_out_35), .row31(n32video_buffer_extendable_2_out_36));
  _32video_buffer_extendable u_32video_buffer_extendable_2 (
    .in_1(abst_obj_1_line_x1), .out_5(n32video_buffer_extendable_2_out_5),
    .out_6(n32video_buffer_extendable_2_out_6), .out_7(n32video_buffer_extendable_2_out_7),
    .out_8(n32video_buffer_extendable_2_out_8), .out_9(n32video_buffer_extendable_2_out_9),
    .out_10(n32video_buffer_extendable_2_out_10), .out_11(n32video_buffer_extendable_2_out_11),
    .out_12(n32video_buffer_extendable_2_out_12), .out_13(n32video_buffer_extendable_2_out_13),
    .out_14(n32video_buffer_extendable_2_out_14), .out_15(n32video_buffer_extendable_2_out_15),
    .out_16(n32video_buffer_extendable_2_out_16), .out_17(n32video_buffer_extendable_2_out_17),
    .out_18(n32video_buffer_extendable_2_out_18), .out_19(n32video_buffer_extendable_2_out_19),
    .out_20(n32video_buffer_extendable_2_out_20), .out_21(n32video_buffer_extendable_2_out_21),
    .out_22(n32video_buffer_extendable_2_out_22), .out_23(n32video_buffer_extendable_2_out_23),
    .out_24(n32video_buffer_extendable_2_out_24), .out_25(n32video_buffer_extendable_2_out_25),
    .out_26(n32video_buffer_extendable_2_out_26), .out_27(n32video_buffer_extendable_2_out_27),
    .out_28(n32video_buffer_extendable_2_out_28), .out_29(n32video_buffer_extendable_2_out_29),
    .out_30(n32video_buffer_extendable_2_out_30), .out_31(n32video_buffer_extendable_2_out_31),
    .out_32(n32video_buffer_extendable_2_out_32), .out_33(n32video_buffer_extendable_2_out_33),
    .out_34(n32video_buffer_extendable_2_out_34), .out_35(n32video_buffer_extendable_2_out_35),
    .out_36(n32video_buffer_extendable_2_out_36), .block(not_2_out), .y(abst_obj_1_cur_line[4:0]),
    .w(comparator_2_eq));
  not not_4 (not_4_out, not_2_out);
  _32video_buffer_extendable u_32video_buffer_extendable_3 (
    .in_1(abst_obj_1_line_x2), .out_5(n32video_buffer_extendable_3_out_5),
    .out_6(n32video_buffer_extendable_3_out_6), .out_7(n32video_buffer_extendable_3_out_7),
    .out_8(n32video_buffer_extendable_3_out_8), .out_9(n32video_buffer_extendable_3_out_9),
    .out_10(n32video_buffer_extendable_3_out_10), .out_11(n32video_buffer_extendable_3_out_11),
    .out_12(n32video_buffer_extendable_3_out_12), .out_13(n32video_buffer_extendable_3_out_13),
    .out_14(n32video_buffer_extendable_3_out_14), .out_15(n32video_buffer_extendable_3_out_15),
    .out_16(n32video_buffer_extendable_3_out_16), .out_17(n32video_buffer_extendable_3_out_17),
    .out_18(n32video_buffer_extendable_3_out_18), .out_19(n32video_buffer_extendable_3_out_19),
    .out_20(n32video_buffer_extendable_3_out_20), .out_21(n32video_buffer_extendable_3_out_21),
    .out_22(n32video_buffer_extendable_3_out_22), .out_23(n32video_buffer_extendable_3_out_23),
    .out_24(n32video_buffer_extendable_3_out_24), .out_25(n32video_buffer_extendable_3_out_25),
    .out_26(n32video_buffer_extendable_3_out_26), .out_27(n32video_buffer_extendable_3_out_27),
    .out_28(n32video_buffer_extendable_3_out_28), .out_29(n32video_buffer_extendable_3_out_29),
    .out_30(n32video_buffer_extendable_3_out_30), .out_31(n32video_buffer_extendable_3_out_31),
    .out_32(n32video_buffer_extendable_3_out_32), .out_33(n32video_buffer_extendable_3_out_33),
    .out_34(n32video_buffer_extendable_3_out_34), .out_35(n32video_buffer_extendable_3_out_35),
    .out_36(n32video_buffer_extendable_3_out_36), .block(not_4_out), .y(abst_obj_1_cur_line[4:0]),
    .w(comparator_2_eq));
  DotMatrix #(.inputtype("row"), .matrixcols(32), .matrixrows(32)) dotmatrix_3 (
    .row0(n32video_buffer_extendable_3_out_5), .row1(n32video_buffer_extendable_3_out_6),
    .row2(n32video_buffer_extendable_3_out_7), .row3(n32video_buffer_extendable_3_out_8),
    .row4(n32video_buffer_extendable_3_out_9), .row5(n32video_buffer_extendable_3_out_10),
    .row6(n32video_buffer_extendable_3_out_11), .row7(n32video_buffer_extendable_3_out_12),
    .row8(n32video_buffer_extendable_3_out_13), .row9(n32video_buffer_extendable_3_out_14),
    .row10(n32video_buffer_extendable_3_out_15), .row11(n32video_buffer_extendable_3_out_16),
    .row12(n32video_buffer_extendable_3_out_17), .row13(n32video_buffer_extendable_3_out_18),
    .row14(n32video_buffer_extendable_3_out_19), .row15(n32video_buffer_extendable_3_out_20),
    .row16(n32video_buffer_extendable_3_out_21), .row17(n32video_buffer_extendable_3_out_22),
    .row18(n32video_buffer_extendable_3_out_23), .row19(n32video_buffer_extendable_3_out_24),
    .row20(n32video_buffer_extendable_3_out_25), .row21(n32video_buffer_extendable_3_out_26),
    .row22(n32video_buffer_extendable_3_out_27), .row23(n32video_buffer_extendable_3_out_28),
    .row24(n32video_buffer_extendable_3_out_29), .row25(n32video_buffer_extendable_3_out_30),
    .row26(n32video_buffer_extendable_3_out_31), .row27(n32video_buffer_extendable_3_out_32),
    .row28(n32video_buffer_extendable_3_out_33), .row29(n32video_buffer_extendable_3_out_34),
    .row30(n32video_buffer_extendable_3_out_35), .row31(n32video_buffer_extendable_3_out_36));
  DotMatrix #(.inputtype("row"), .matrixcols(32), .matrixrows(32)) dotmatrix_4 (
    .row0(n32video_buffer_extendable_4_out_5), .row1(n32video_buffer_extendable_4_out_6),
    .row2(n32video_buffer_extendable_4_out_7), .row3(n32video_buffer_extendable_4_out_8),
    .row4(n32video_buffer_extendable_4_out_9), .row5(n32video_buffer_extendable_4_out_10),
    .row6(n32video_buffer_extendable_4_out_11), .row7(n32video_buffer_extendable_4_out_12),
    .row8(n32video_buffer_extendable_4_out_13), .row9(n32video_buffer_extendable_4_out_14),
    .row10(n32video_buffer_extendable_4_out_15), .row11(n32video_buffer_extendable_4_out_16),
    .row12(n32video_buffer_extendable_4_out_17), .row13(n32video_buffer_extendable_4_out_18),
    .row14(n32video_buffer_extendable_4_out_19), .row15(n32video_buffer_extendable_4_out_20),
    .row16(n32video_buffer_extendable_4_out_21), .row17(n32video_buffer_extendable_4_out_22),
    .row18(n32video_buffer_extendable_4_out_23), .row19(n32video_buffer_extendable_4_out_24),
    .row20(n32video_buffer_extendable_4_out_25), .row21(n32video_buffer_extendable_4_out_26),
    .row22(n32video_buffer_extendable_4_out_27), .row23(n32video_buffer_extendable_4_out_28),
    .row24(n32video_buffer_extendable_4_out_29), .row25(n32video_buffer_extendable_4_out_30),
    .row26(n32video_buffer_extendable_4_out_31), .row27(n32video_buffer_extendable_4_out_32),
    .row28(n32video_buffer_extendable_4_out_33), .row29(n32video_buffer_extendable_4_out_34),
    .row30(n32video_buffer_extendable_4_out_35), .row31(n32video_buffer_extendable_4_out_36));
  _32video_buffer_extendable u_32video_buffer_extendable_4 (
    .in_1(abst_obj_1_line_x2), .out_5(n32video_buffer_extendable_4_out_5),
    .out_6(n32video_buffer_extendable_4_out_6), .out_7(n32video_buffer_extendable_4_out_7),
    .out_8(n32video_buffer_extendable_4_out_8), .out_9(n32video_buffer_extendable_4_out_9),
    .out_10(n32video_buffer_extendable_4_out_10), .out_11(n32video_buffer_extendable_4_out_11),
    .out_12(n32video_buffer_extendable_4_out_12), .out_13(n32video_buffer_extendable_4_out_13),
    .out_14(n32video_buffer_extendable_4_out_14), .out_15(n32video_buffer_extendable_4_out_15),
    .out_16(n32video_buffer_extendable_4_out_16), .out_17(n32video_buffer_extendable_4_out_17),
    .out_18(n32video_buffer_extendable_4_out_18), .out_19(n32video_buffer_extendable_4_out_19),
    .out_20(n32video_buffer_extendable_4_out_20), .out_21(n32video_buffer_extendable_4_out_21),
    .out_22(n32video_buffer_extendable_4_out_22), .out_23(n32video_buffer_extendable_4_out_23),
    .out_24(n32video_buffer_extendable_4_out_24), .out_25(n32video_buffer_extendable_4_out_25),
    .out_26(n32video_buffer_extendable_4_out_26), .out_27(n32video_buffer_extendable_4_out_27),
    .out_28(n32video_buffer_extendable_4_out_28), .out_29(n32video_buffer_extendable_4_out_29),
    .out_30(n32video_buffer_extendable_4_out_30), .out_31(n32video_buffer_extendable_4_out_31),
    .out_32(n32video_buffer_extendable_4_out_32), .out_33(n32video_buffer_extendable_4_out_33),
    .out_34(n32video_buffer_extendable_4_out_34), .out_35(n32video_buffer_extendable_4_out_35),
    .out_36(n32video_buffer_extendable_4_out_36), .block(not_2_out), .y(abst_obj_1_cur_line[4:0]),
    .w(comparator_2_eq));

  // Other names for the same wires on the sheet: IDin[15:0] = id

  // Notes on the sheet:
  //   texture line counter
  //   Схема противников
  //   contents of rom_1 (hex, n*v repeats v):
  //   2 7 5 2 4*5 7 2 7 7 2 5 7 5 5 2 1 1 1
endmodule

module abstobj2 (
  input  write,
  input  [4:0] texture_line,
  input  [31:0] texture_input,
  input  [6:0] x,
  input  [6:0] y,
  input  draw,
  output [31:0] line_x1,
  output [31:0] line_x2,
  output drawing,
  output [5:0] cur_line
);

  wire _0__y_line_32, and_2_out, and_3_out, clock_1_out, clock_2_out, comparator_1_eq, comparator_2_lt,
       counter_1_carry, not_1_out, not_2_out, not_4_out, subtractor_2_bout, subtractor_3_bout,
       transistor_3_out, x_32, x__0;
  wire [4:0] bit_extender_3_out, bit_extender_5_out, counter_1_q, multiplexer_1_out, multiplexer_2_out,
       multiplexer_4_out, subtractor_3_out, subtractor_4_out, transistor_1_out;
  wire [5:0] adder_1_out, bit_extender_1_out, bit_extender_2_out, bit_extender_4_out, subtractor_1_out,
       subtractor_2_out;
  wire [31:0] n32_bit_reverse_1_out_2, ram_1_data, shifter_1_out, shifter_2_out, shifter_3_out;

  // Probe on x
  // Probe on y
  Register #(.width(6)) register_1 (.D(adder_1_out), .Q(cur_line), .clk(clock_1_out), .clr(not_1_out));  // open: en
  not not_1 (not_1_out, drawing);
  Clock clock_1 (.out(clock_1_out));
  Bit_Extender #(.in_width(7), .out_width(6)) bit_extender_1 (.in(x), .out(bit_extender_1_out));
  Bit_Extender #(.in_width(7), .out_width(6)) bit_extender_2 (.in(y), .out(bit_extender_2_out));
  Bit_Extender #(.in_width(6), .out_width(5)) bit_extender_3 (.in(subtractor_1_out), .out(bit_extender_3_out));
  Subtractor #(.width(6)) subtractor_1 (
    .a(adder_1_out), .b(bit_extender_2_out), .out(subtractor_1_out));  // open: bin, bout
  Comparator #(.width(6), .mode("unsigned")) comparator_1 (
    .a(bit_extender_1_out), .b({6{1'b0}}), .eq(comparator_1_eq));  // open: gt, lt
  Counter #(.width(5), .max('h3)) counter_1 (
    .count(drawing), .Q(counter_1_q), .carry(counter_1_carry), .clk(not_2_out), .clr(counter_1_carry));  // open: load, D
  not not_2 (not_2_out, clock_2_out);
  Clock clock_2 (.out(clock_2_out));
  Subtractor #(.width(6)) subtractor_2 (
    .a(adder_1_out), .b(bit_extender_2_out), .out(subtractor_2_out), .bout(subtractor_2_bout));  // open: bin
  Transistor #(.gate("br"), .width(5)) transistor_1 (.in(texture_line), .out(transistor_1_out), .gate(drawing));
  Transistor #(.\type ("n"), .width(5)) transistor_2 (.in(bit_extender_3_out), .out(transistor_1_out), .gate(drawing));
  not not_3 (x__0, comparator_1_eq);
  assign bit_extender_4_out = {{1{1'b0}}, counter_1_q};  // Bit_Extender bit_extender_4
  Comparator #(.width(6), .mode("unsigned")) comparator_2 (
    .a(subtractor_2_out), .b(6'b100000), .lt(comparator_2_lt));  // open: gt, eq
  not not_4 (not_4_out, subtractor_2_bout);
  Counter #(.width(1), .max('h1)) tmp (.Q(drawing), .clk(draw), .clr(counter_1_carry));  // open: load, D, count, carry
  Transistor #(.gate("br")) transistor_3 (.in(write), .out(transistor_3_out), .gate(drawing));
  not not_5 (x_32, bit_extender_1_out[5]);
  Adder #(.width(6)) adder_1 (.a(bit_extender_2_out), .b(bit_extender_4_out), .out(adder_1_out));  // open: cin, cout
  and and_1 (_0__y_line_32, comparator_2_lt, not_4_out);
  assign bit_extender_5_out = {{4{1'b0}}, x_32};  // Bit_Extender bit_extender_5
  _32_bit_reverse u_32_bit_reverse_1 (.in_1(ram_1_data), .out_2(n32_bit_reverse_1_out_2));
  RAM #(.addrWidth(5), .dataWidth(32), .bus("separate")) ram_1 (
    .addr(transistor_1_out), .din(texture_input), .data(ram_1_data), .clk(transistor_3_out));  // open: str, sel, ld, clr
  Subtractor #(.width(5)) subtractor_3 (
    .a(bit_extender_1_out[4:0]), .b(bit_extender_5_out), .out(subtractor_3_out), .bout(subtractor_3_bout));  // open: bin
  Multiplexer #(.width(5), .enable("false")) multiplexer_1 (
    .in0(subtractor_3_out), .in1({5{1'b0}}), .out(multiplexer_1_out), .sel(subtractor_3_bout));
  // Probe on {5{1'b1}}
  // Probe on subtractor_4_out
  Subtractor #(.width(5)) subtractor_4 (
    .a({5{1'b1}}), .b(multiplexer_1_out), .out(subtractor_4_out));  // open: bin, bout
  Shifter #(.width(32), .shift("lr")) shifter_1 (
    .in(n32_bit_reverse_1_out_2), .\dist (bit_extender_1_out[4:0]), .out(shifter_1_out));
  Multiplexer #(.width(5), .enable("false")) multiplexer_2 (
    .in0({5{1'b0}}), .in1(subtractor_4_out), .out(multiplexer_2_out), .sel(x_32));
  and and_2 (and_2_out, x_32, drawing, _0__y_line_32);
  Multiplexer #(.width(32), .enable("false")) multiplexer_3 (
    .in0({32{1'b0}}), .in1(shifter_1_out), .out(line_x1), .sel(and_2_out));
  Shifter #(.width(32)) shifter_2 (.in(n32_bit_reverse_1_out_2), .\dist (multiplexer_2_out), .out(shifter_2_out));
  Multiplexer #(.width(5), .enable("false")) multiplexer_4 (
    .in0(bit_extender_1_out[4:0]), .in1({5{1'b0}}), .out(multiplexer_4_out), .sel(x_32));
  Shifter #(.width(32), .shift("lr")) shifter_3 (.in(shifter_2_out), .\dist (multiplexer_4_out), .out(shifter_3_out));
  and and_3 (and_3_out, x__0, drawing, _0__y_line_32);
  Multiplexer #(.width(32), .enable("false")) multiplexer_5 (
    .in0({32{1'b0}}), .in1(shifter_3_out), .out(line_x2), .sel(and_3_out));

  // Notes on the sheet:
  //   address = line-y
  //   if x=0 shift left for line x2 must be 32 (with simulation of 32 shift)
  //   shift left for line x2
  //   shift rigth for line x2
  //   shift right works only if shift left = 0
endmodule

module enemies (
  input  collide,
  input  \wait ,
  input  draw,
  input  clock,
  output [15:0] id,
  output initing,
  output [15:0] y,
  output [4:0] DEBUG__enemy_cout,
  output [15:0] x,
  output [15:0] command,
  output ready
);

  wire and_1_out, and_3_out, clock_1_out, clock_2_out, comparator_1_eq, comparator_2_eq, counter_1_carry,
       counter_3_q, draw_t, multiplexer_1_out, multiplexer_3_out, not_1_out, not_3_out, not_4_out, or_2_out,
       or_3_out, pull_resistor_2_node, ram_1_data, ready_t, register_1_q, register_3_q, texture_state,
       transistor_1_out, wait_t, xnor_1_out;
  wire [15:0] adder_1_out, adder_2_out, adder_3_out, adder_4_out, adder_5_out, adder_6_out,
       bit_extender_1_out, bit_extender_2_out, divider_1_out, divider_1_rem, multiplexer_2_out,
       multiplexer_4_out, multiplier_1_out, multiplier_2_out, negator_1_out, x_t, y_t;

  or or_1 (wait_t, collide, \wait );
  Register #(.width(1)) register_1 (.D(draw), .Q(register_1_q), .clk(draw), .clr(ready_t));  // open: en
  Register #(.width(1)) register_2 (.D(register_1_q), .Q(draw_t), .clk(clock_1_out), .clr(ready_t));  // open: en
  Clock clock_1 (.out(clock_1_out));
  not not_1 (not_1_out, multiplexer_1_out);
  Multiplexer #(.enable("false")) multiplexer_1 (
    .in0(clock), .in1(transistor_1_out), .out(multiplexer_1_out), .sel(register_3_q));
  Transistor #(.\type ("n"), .gate("br")) transistor_1 (.in(wait_t), .out(transistor_1_out), .gate(draw_t));
  Pull_Resistor pull_resistor_1 (.node(transistor_1_out));
  not not_2 (initing, register_3_q);
  Counter #(.width(5), .max('he)) counter_1 (
    .Q(DEBUG__enemy_cout), .carry(counter_1_carry), .clk(not_1_out));  // open: load, D, count, clr
  not not_3 (not_3_out, counter_1_carry);
  Register #(.width(1)) register_3 (.D(not_3_out), .Q(register_3_q), .clk(not_3_out));  // open: en, clr
  Pull_Resistor pull_resistor_2 (.node(pull_resistor_2_node));
  Transistor #(.gate("br")) transistor_2 (.in(1'b1), .out(pull_resistor_2_node), .gate(register_3_q));
  Negator #(.width(16)) negator_1 (.in(16'h2), .out(negator_1_out));
  assign bit_extender_1_out = {{11{1'b0}}, DEBUG__enemy_cout};  // Bit_Extender bit_extender_1
  Clock clock_2 (.out(clock_2_out));
  xnor xnor_1 (xnor_1_out, collide, register_3_q);
  Adder #(.width(16)) adder_1 (.a(x_t), .b(multiplexer_2_out), .out(adder_1_out));  // open: cin, cout
  Multiplexer #(.width(16), .enable("false")) multiplexer_2 (
    .in0(16'h2), .in1(negator_1_out), .out(multiplexer_2_out), .sel(counter_3_q));
  Adder #(.width(16)) adder_2 (.a(16'h2), .b(y_t), .out(adder_2_out));  // open: cin, cout
  RAM #(.addrWidth(5), .dataWidth(1), .bus("separate")) ram_1 (
    .addr(DEBUG__enemy_cout), .din(pull_resistor_2_node), .data(ram_1_data), .str(xnor_1_out),
    .clk(clock_2_out));  // open: sel, ld, clr
  Register #(.width(1)) register_4 (.D(not_3_out), .Q(ready_t), .clk(not_3_out), .clr(ready_t));  // open: en
  Register #(.width(16)) register_5 (.D(adder_1_out), .Q(x_t), .clk(ready_t));  // open: en, clr
  Register #(.width(16)) register_6 (.D(adder_2_out), .Q(y_t), .clk(comparator_2_eq));  // open: en, clr
  Divider #(.width(16)) divider_1 (
    .a(bit_extender_1_out), .b(16'h5), .out(divider_1_out), .rem(divider_1_rem));  // open: upper
  and and_1 (and_1_out, ram_1_data, register_3_q);
  and and_2 (ready, ready_t, draw_t);
  Comparator #(.width(16), .mode("unsigned")) comparator_1 (.a(x_t), .b(16'h12), .eq(comparator_1_eq));  // open: gt, lt
  and and_3 (and_3_out, and_1_out, or_2_out);
  not not_4 (not_4_out, clock);
  Adder #(.width(16)) adder_3 (.a(16'h3), .b(divider_1_out), .out(adder_3_out));  // open: cin, cout
  Adder #(.width(16)) adder_4 (.a(16'h6), .b(divider_1_out), .out(adder_4_out));  // open: cin, cout
  Multiplier #(.width(16)) multiplier_1 (.a(divider_1_out), .b(16'ha), .out(multiplier_1_out));  // open: cin, cout
  Multiplier #(.width(16)) multiplier_2 (.a(divider_1_rem), .b(16'ha), .out(multiplier_2_out));  // open: cin, cout
  Multiplexer #(.enable("false")) multiplexer_3 (.in0(1'b0), .in1(1'b1), .out(multiplexer_3_out), .sel(and_3_out));
  or or_2 (or_2_out, not_4_out, wait_t);
  Counter #(.width(1), .max('h1)) counter_2 (.Q(texture_state), .clk(ready_t));  // open: load, D, count, carry, clr
  Comparator #(.width(16), .mode("unsigned")) comparator_2 (
    .a(x_t), .b({16{1'b0}}), .eq(comparator_2_eq));  // open: gt, lt
  Multiplexer #(.width(16), .enable("false")) multiplexer_4 (
    .in0(adder_3_out), .in1(adder_4_out), .out(multiplexer_4_out), .sel(texture_state));
  Adder #(.width(16)) adder_5 (.a(y_t), .b(multiplier_1_out), .out(adder_5_out));  // open: cin, cout
  Adder #(.width(16)) adder_6 (.a(x_t), .b(multiplier_2_out), .out(adder_6_out));  // open: cin, cout
  assign bit_extender_2_out = {{15{1'b0}}, multiplexer_3_out};  // Bit_Extender bit_extender_2
  Counter #(.width(1), .max('h1)) counter_3 (.Q(counter_3_q), .clk(or_3_out));  // open: load, D, count, carry, clr
  or or_3 (or_3_out, comparator_2_eq, comparator_1_eq);
  assign id = draw_t ? multiplexer_4_out : 16'bz;  // Controlled_Buffer controlled_buffer_1
  assign y = draw_t ? adder_5_out : 16'bz;  // Controlled_Buffer controlled_buffer_2
  assign x = draw_t ? adder_6_out : 16'bz;  // Controlled_Buffer controlled_buffer_3
  assign command = draw_t ? bit_extender_2_out : 16'bz;  // Controlled_Buffer controlled_buffer_4

  // Other names for the same wires on the sheet: clk = clock; col = collide

  // Notes on the sheet:
  //   enemy matrix
  //   enemies in row
  //   base texture id1
  //   base texture id2
  //   rows delta
  //   columns delta
  //   output X
  //   output Y
endmodule

module newmain (
);

  wire abst_obj_1_drawing, and_1_out, clk, cmd_show, comparator_1_eq, comparator_2_eq, counter_1_carry,
       not_1_out, not_2_out, not_3_out, or_1_out, or_2_out, pull_resistor_1_node, register_1_q, register_2_q,
       register_4_q, xor_1_out;
  wire [2:0] joystick_1_x, joystick_1_y;
  wire [4:0] counter_1_q;
  wire [5:0] abst_obj_1_cur_line;
  wire [6:0] \схема_расчётов_1_x , \схема_расчётов_1_y ;
  wire [15:0] adder_1_out, bit_extender_1_out, multiplier_1_out, register_3_q, \схема_расчётов_1_command ,
       \схема_расчётов_1_id ;
  wire [31:0] abst_obj_1_line_x1, abst_obj_1_line_x2, n32video_buffer_extendable_1_out_5,
       n32video_buffer_extendable_1_out_6, n32video_buffer_extendable_1_out_7,
       n32video_buffer_extendable_1_out_8, n32video_buffer_extendable_1_out_9,
       n32video_buffer_extendable_1_out_10, n32video_buffer_extendable_1_out_11,
       n32video_buffer_extendable_1_out_12, n32video_buffer_extendable_1_out_13,
       n32video_buffer_extendable_1_out_14, n32video_buffer_extendable_1_out_15,
       n32video_buffer_extendable_1_out_16, n32video_buffer_extendable_1_out_17,
       n32video_buffer_extendable_1_out_18, n32video_buffer_extendable_1_out_19,
       n32video_buffer_extendable_1_out_20, n32video_buffer_extendable_1_out_21,
       n32video_buffer_extendable_1_out_22, n32video_buffer_extendable_1_out_23,
       n32video_buffer_extendable_1_out_24, n32video_buffer_extendable_1_out_25,
       n32video_buffer_extendable_1_out_26, n32video_buffer_extendable_1_out_27,
       n32video_buffer_extendable_1_out_28, n32video_buffer_extendable_1_out_29,
       n32video_buffer_extendable_1_out_30, n32video_buffer_extendable_1_out_31,
       n32video_buffer_extendable_1_out_32, n32video_buffer_extendable_1_out_33,
       n32video_buffer_extendable_1_out_34, n32video_buffer_extendable_1_out_35,
       n32video_buffer_extendable_1_out_36, rom_1_data;

  Clock clock_1 (.out(clk));
  abst_obj abst_obj_1 (
    .y(\схема_расчётов_1_y ), .texture_line(counter_1_q), .write(xor_1_out), .texture_input(rom_1_data),
    .draw(or_1_out), .cur_line(abst_obj_1_cur_line), .line_x1(abst_obj_1_line_x1),
    .line_x2(abst_obj_1_line_x2), .x(\схема_расчётов_1_x ), .drawing(abst_obj_1_drawing));
  Pull_Resistor pull_resistor_1 (.node(pull_resistor_1_node));
  Transistor #(.\type ("n"), .gate("br")) transistor_1 (.in(clk), .out(pull_resistor_1_node), .gate(register_2_q));
  xor xor_1 (xor_1_out, pull_resistor_1_node, register_2_q);
  Counter #(.width(5), .max('h3)) counter_1 (
    .Q(counter_1_q), .carry(counter_1_carry), .clk(pull_resistor_1_node), .clr(or_1_out));  // open: load, D, count
  or or_1 (or_1_out, counter_1_carry, and_1_out);
  Register #(.width(1)) register_1 (
    .D(comparator_2_eq), .Q(register_1_q), .clk(comparator_2_eq), .clr(abst_obj_1_drawing));  // open: en
  not not_1 (not_1_out, clk);
  Register #(.width(1)) register_2 (
    .D(register_1_q), .Q(register_2_q), .clk(not_1_out), .clr(abst_obj_1_drawing));  // open: en
  or or_2 (or_2_out, register_2_q, register_1_q, abst_obj_1_drawing);
  assign bit_extender_1_out = {{11{1'b0}}, counter_1_q};  // Bit_Extender bit_extender_1
  \Схема_расчётов  \u_схема_расчётов_1  (
    .player_inp_x(joystick_1_x), .player_inp_y(joystick_1_y), .ID(\схема_расчётов_1_id ),
    .X(\схема_расчётов_1_x ), .Y(\схема_расчётов_1_y ), .Command(\схема_расчётов_1_command ), .clock(clk),
    .drawing(or_2_out));
  Joystick #(.bits(3)) joystick_1 (.x(joystick_1_x), .y(joystick_1_y));
  // Probe on abst_obj_1_cur_line
  // Probe on \схема_расчётов_1_id 
  Register #(.width(16)) register_3 (
    .D(\схема_расчётов_1_id ), .Q(register_3_q), .clk(abst_obj_1_drawing));  // open: en, clr
  Multiplier #(.width(16)) multiplier_1 (
    .a(\схема_расчётов_1_id ), .b(16'h3), .out(multiplier_1_out));  // open: cin, cout
  Comparator #(.width(16), .mode("unsigned")) comparator_1 (
    .a(\схема_расчётов_1_id ), .b(register_3_q), .eq(comparator_1_eq));  // open: gt, lt
  Register #(.width(1)) register_4 (
    .D(abst_obj_1_drawing), .Q(register_4_q), .clk(abst_obj_1_drawing));  // open: en, clr
  Comparator #(.width(16), .mode("unsigned")) comparator_2 (
    .a(\схема_расчётов_1_command ), .b(16'h1), .eq(comparator_2_eq));  // open: gt, lt
  Pull_Resistor pull_resistor_2 (.node(comparator_2_eq));
  Comparator #(.width(16), .mode("unsigned")) comparator_3 (
    .a(\схема_расчётов_1_command ), .b(16'h2), .eq(cmd_show));  // open: gt, lt
  and and_1 (and_1_out, comparator_2_eq, register_4_q, comparator_1_eq);
  not not_2 (not_2_out, abst_obj_1_cur_line[5]);
  Adder #(.width(16)) adder_1 (.a(bit_extender_1_out), .b(multiplier_1_out), .out(adder_1_out));  // open: cin, cout
  Pull_Resistor pull_resistor_3 (.node(comparator_1_eq));
  ROM #(.addrWidth(16), .dataWidth(32)) rom_1 (.addr(adder_1_out), .data(rom_1_data));  // open: sel
  DotMatrix #(.inputtype("row"), .matrixcols(32), .matrixrows(32)) dotmatrix_1 (
    .row0(n32video_buffer_extendable_1_out_5), .row1(n32video_buffer_extendable_1_out_6),
    .row2(n32video_buffer_extendable_1_out_7), .row3(n32video_buffer_extendable_1_out_8),
    .row4(n32video_buffer_extendable_1_out_9), .row5(n32video_buffer_extendable_1_out_10),
    .row6(n32video_buffer_extendable_1_out_11), .row7(n32video_buffer_extendable_1_out_12),
    .row8(n32video_buffer_extendable_1_out_13), .row9(n32video_buffer_extendable_1_out_14),
    .row10(n32video_buffer_extendable_1_out_15), .row11(n32video_buffer_extendable_1_out_16),
    .row12(n32video_buffer_extendable_1_out_17), .row13(n32video_buffer_extendable_1_out_18),
    .row14(n32video_buffer_extendable_1_out_19), .row15(n32video_buffer_extendable_1_out_20),
    .row16(n32video_buffer_extendable_1_out_21), .row17(n32video_buffer_extendable_1_out_22),
    .row18(n32video_buffer_extendable_1_out_23), .row19(n32video_buffer_extendable_1_out_24),
    .row20(n32video_buffer_extendable_1_out_25), .row21(n32video_buffer_extendable_1_out_26),
    .row22(n32video_buffer_extendable_1_out_27), .row23(n32video_buffer_extendable_1_out_28),
    .row24(n32video_buffer_extendable_1_out_29), .row25(n32video_buffer_extendable_1_out_30),
    .row26(n32video_buffer_extendable_1_out_31), .row27(n32video_buffer_extendable_1_out_32),
    .row28(n32video_buffer_extendable_1_out_33), .row29(n32video_buffer_extendable_1_out_34),
    .row30(n32video_buffer_extendable_1_out_35), .row31(n32video_buffer_extendable_1_out_36));
  _32video_buffer_extendable u_32video_buffer_extendable_1 (
    .in_1(abst_obj_1_line_x1), .out_5(n32video_buffer_extendable_1_out_5),
    .out_6(n32video_buffer_extendable_1_out_6), .out_7(n32video_buffer_extendable_1_out_7),
    .out_8(n32video_buffer_extendable_1_out_8), .out_9(n32video_buffer_extendable_1_out_9),
    .out_10(n32video_buffer_extendable_1_out_10), .out_11(n32video_buffer_extendable_1_out_11),
    .out_12(n32video_buffer_extendable_1_out_12), .out_13(n32video_buffer_extendable_1_out_13),
    .out_14(n32video_buffer_extendable_1_out_14), .out_15(n32video_buffer_extendable_1_out_15),
    .out_16(n32video_buffer_extendable_1_out_16), .out_17(n32video_buffer_extendable_1_out_17),
    .out_18(n32video_buffer_extendable_1_out_18), .out_19(n32video_buffer_extendable_1_out_19),
    .out_20(n32video_buffer_extendable_1_out_20), .out_21(n32video_buffer_extendable_1_out_21),
    .out_22(n32video_buffer_extendable_1_out_22), .out_23(n32video_buffer_extendable_1_out_23),
    .out_24(n32video_buffer_extendable_1_out_24), .out_25(n32video_buffer_extendable_1_out_25),
    .out_26(n32video_buffer_extendable_1_out_26), .out_27(n32video_buffer_extendable_1_out_27),
    .out_28(n32video_buffer_extendable_1_out_28), .out_29(n32video_buffer_extendable_1_out_29),
    .out_30(n32video_buffer_extendable_1_out_30), .out_31(n32video_buffer_extendable_1_out_31),
    .out_32(n32video_buffer_extendable_1_out_32), .out_33(n32video_buffer_extendable_1_out_33),
    .out_34(n32video_buffer_extendable_1_out_34), .out_35(n32video_buffer_extendable_1_out_35),
    .out_36(n32video_buffer_extendable_1_out_36), .block(not_3_out), .y(abst_obj_1_cur_line[4:0]),
    .w(cmd_show));
  not not_3 (not_3_out, not_2_out);

  // Notes on the sheet:
  //   texture line counter
  //   contents of rom_1 (hex, n*v repeats v):
  //   2 7 5 2 5 5 0 0 0 2 7 5 2 5 5 7 5 5 2 7 7 2 5 7 2 5 5
endmodule

module pos_writer (
  input  [15:0] x,
  input  [5:0] int_vec,
  input  [15:0] y,
  input  run,
  input  clock,
  output [15:0] adr,
  output [15:0] val,
  output [5:0] int_vec_2,
  output write,
  output IRQ
);

  wire counter_1_carry, not_1_out, not_2_out, writing;
  wire [1:0] bit_extender_1_out, register_1_q;
  wire [2:0] counter_1_q;
  wire [15:0] multiplexer_1_out, multiplexer_2_out;

  Counter #(.width(3), .max('h4)) counter_1 (
    .Q(counter_1_q), .carry(counter_1_carry), .clk(clock), .clr(not_2_out));  // open: load, D, count
  // Probe on x
  // Probe on y
  Bit_Extender #(.in_width(3), .out_width(2)) bit_extender_1 (.in(counter_1_q), .out(bit_extender_1_out));
  Register #(.width(2)) register_1 (
    .D(bit_extender_1_out), .Q(register_1_q), .clk(not_1_out), .clr(not_2_out));  // open: en
  not not_1 (not_1_out, clock);
  Multiplexer #(.select(2), .width(16), .enable("false")) multiplexer_1 (
    .in0({16{1'b0}}), .in1(16'h80), .in2(16'h82), .in3(16'h84), .out(multiplexer_1_out), .sel(register_1_q));
  Multiplexer #(.select(2), .width(16), .enable("false")) multiplexer_2 (
    .in0({16{1'b0}}), .in1(x), .in2(y), .in3(16'h1), .out(multiplexer_2_out), .sel(bit_extender_1_out));
  // Probe on multiplexer_1_out
  assign adr = writing ? multiplexer_1_out : 16'bz;  // Controlled_Buffer controlled_buffer_1
  assign val = writing ? multiplexer_2_out : 16'bz;  // Controlled_Buffer controlled_buffer_2
  // Probe on multiplexer_2_out
  not not_2 (not_2_out, writing);
  Transistor #(.\type ("n"), .gate("br")) transistor_1 (.in(writing), .out(write), .gate(writing));
  Register #(.width(1)) register_2 (.D(run), .Q(writing), .clk(run), .clr(counter_1_carry));  // open: en
  assign int_vec_2 = writing ? int_vec : 6'bz;  // Controlled_Buffer controlled_buffer_3
  assign IRQ = writing ? 1'b0 : 1'bz;  // Controlled_Buffer controlled_buffer_4

  // Other names for the same wires on the sheet: clk = clock
endmodule

module player (
  input  [15:0] x,
  input  [15:0] y,
  input  \wait ,
  input  draw,
  input  clock,
  output [15:0] id,
  output [15:0] x_2,
  output [15:0] y_2,
  output [15:0] command,
  output ready
);

  wire and_1_out, comparator_1_eq, draw_t, not_1_out, transistor_1_out;
  wire [1:0] counter_1_q;
  wire [15:0] adder_1_out, adder_2_out, bit_extender_1_out, x_q, y_q;

  not not_1 (not_1_out, \wait );
  Register #(.width(1)) register_1 (.D(draw), .Q(draw_t), .clk(draw), .clr(ready));  // open: en
  Counter #(.width(2), .max('h3)) counter_1 (
    .Q(counter_1_q), .carry(ready), .clk(transistor_1_out), .clr(ready));  // open: load, D, count
  Transistor #(.\type ("n")) transistor_1 (.in(clock), .out(transistor_1_out), .gate(and_1_out));
  and and_1 (and_1_out, not_1_out, draw_t);
  Adder #(.width(16)) adder_1 (.a(x_q), .b(x), .out(adder_1_out));  // open: cin, cout
  Adder #(.width(16)) adder_2 (.a(y_q), .b(y), .out(adder_2_out));  // open: cin, cout
  Comparator #(.width(2), .mode("unsigned")) comparator_1 (
    .a(counter_1_q), .b(2'b01), .eq(comparator_1_eq));  // open: gt, lt
  Register #(.width(16)) u_x (.D(adder_1_out), .Q(x_q), .clk(draw_t));  // open: en, clr
  Register #(.width(16)) u_y (.D(adder_2_out), .Q(y_q), .clk(draw_t));  // open: en, clr
  assign bit_extender_1_out = {{15{1'b0}}, comparator_1_eq};  // Bit_Extender bit_extender_1
  assign id = draw_t ? {16{1'b0}} : 16'bz;  // Controlled_Buffer controlled_buffer_1
  assign x_2 = draw_t ? x_q : 16'bz;  // Controlled_Buffer controlled_buffer_2
  assign y_2 = draw_t ? y_q : 16'bz;  // Controlled_Buffer controlled_buffer_3
  assign command = draw_t ? bit_extender_1_out : 16'bz;  // Controlled_Buffer controlled_buffer_4

  // Other names for the same wires on the sheet: clk = clock
endmodule

module \Схема_расчётов  (
  input  [2:0] player_inp_x,
  input  [2:0] player_inp_y,
  input  drawing,
  input  clock,
  output [6:0] X,
  output [6:0] Y,
  output [15:0] Command,
  output [15:0] ID
);

  wire cheker_write_2_1_write, comparator_1_eq, comparator_2_eq, comparator_3_eq, comparator_4_eq,
       comparator_5_eq, counter_1_carry, enemies_1_ready, hold, not_1_out, or_1_out, or_2_out,
       player_1_ready, register_1_q, transistor_1_out;
  wire [4:0] enemies_1_debug__enemy_cout;
  wire [15:0] bit_extender_1_out, bit_extender_2_out, cdm16_1_cheker, cdm16_1_collide, cdm16_1_run,
       cheker_write_2_1_adr, cheker_write_2_1_val, divider_1_out, divider_2_out, player_1_command,
       player_1_x_2, player_1_y_2, subtractor_1_out, subtractor_2_out;

  assign bit_extender_1_out = {{13{1'b0}}, player_inp_x};  // Bit_Extender bit_extender_1
  assign bit_extender_2_out = {{13{1'b0}}, player_inp_y};  // Bit_Extender bit_extender_2
  Transistor #(.\type ("n"), .gate("br")) transistor_1 (.in(clock), .out(transistor_1_out), .gate(register_1_q));
  Subtractor #(.width(16)) subtractor_1 (.a(bit_extender_1_out), .b(16'h4), .out(subtractor_1_out));  // open: bin, bout
  Subtractor #(.width(16)) subtractor_2 (.a(bit_extender_2_out), .b(16'h4), .out(subtractor_2_out));  // open: bin, bout
  Counter #(.width(2), .max('h3)) counter_1 (
    .carry(counter_1_carry), .clk(transistor_1_out), .clr(counter_1_carry));  // open: load, D, count, Q
  player player_1 (
    .draw(counter_1_carry), .ready(player_1_ready), .id(ID), .x_2(player_1_x_2), .y_2(player_1_y_2),
    .x(subtractor_1_out), .y(subtractor_2_out), .command(player_1_command), .\wait (or_2_out), .clock(clock));
  // Probe on enemies_1_debug__enemy_cout
  enemies enemies_1 (
    .\wait (or_2_out), .draw(player_1_ready), .id(ID), .y(player_1_y_2), .x(player_1_x_2),
    .command(player_1_command), .ready(enemies_1_ready), .initing(hold), .collide(comparator_3_eq),
    .clock(clock), .DEBUG__enemy_cout(enemies_1_debug__enemy_cout));
  or or_1 (or_1_out, comparator_4_eq, comparator_1_eq);
  Register #(.width(1)) register_1 (.D(or_1_out), .Q(register_1_q), .clk(or_1_out), .clr(counter_1_carry));  // open: en
  Comparator #(.width(16), .mode("unsigned")) comparator_1 (
    .a(player_1_command), .b(16'h2), .eq(comparator_1_eq));  // open: gt, lt
  Pull_Resistor pull_resistor_1 (.node(comparator_1_eq));
  Comparator #(.width(16), .mode("unsigned")) comparator_2 (
    .a(player_1_command), .b(16'h1), .eq(comparator_2_eq));  // open: gt, lt
  Pull_Resistor pull_resistor_2 (.node(comparator_2_eq));
  or or_2 (or_2_out, cheker_write_2_1_write, comparator_5_eq, drawing);
  Bit_Extender #(.in_width(16), .out_width(7)) bit_extender_3 (.in(divider_1_out), .out(X));
  Divider #(.width(16)) divider_1 (.a(player_1_x_2), .b(16'h2), .out(divider_1_out));  // open: upper, rem
  Divider #(.width(16)) divider_2 (.a(player_1_y_2), .b(16'h2), .out(divider_2_out));  // open: upper, rem
  cheker_write_2 cheker_write_2_1 (
    .adr(cheker_write_2_1_adr), .val(cheker_write_2_1_val), .write(cheker_write_2_1_write),
    .run(enemies_1_ready), .clock(clock));  // open: int_vec, int_vec_2, IRQ
  pos_writer pos_writer_1 (
    .x(player_1_x_2), .y(player_1_y_2), .adr(cheker_write_2_1_adr), .val(cheker_write_2_1_val),
    .write(cheker_write_2_1_write), .run(comparator_2_eq), .clock(clock));  // open: int_vec_2, IRQ, int_vec
  Pull_Resistor pull_resistor_3 (.node(cheker_write_2_1_write));
  Bit_Extender #(.in_width(16), .out_width(7)) bit_extender_4 (.in(divider_2_out), .out(Y));
  CDM16 cdm16_1 (
    .adr(cheker_write_2_1_adr), .val(cheker_write_2_1_val), .id(ID), .x(player_1_x_2), .y(player_1_y_2),
    .command(player_1_command), .collide(cdm16_1_collide), .write(cheker_write_2_1_write), .hold(hold),
    .clock(clock), .draw(enemies_1_ready), .cheker(cdm16_1_cheker), .run(cdm16_1_run));
  Comparator #(.width(16), .mode("unsigned")) comparator_3 (
    .a(cdm16_1_collide), .b(16'h1), .eq(comparator_3_eq));  // open: gt, lt
  // Probe on cdm16_1_cheker
  assign Command = not_1_out ? player_1_command : 16'bz;  // Controlled_Buffer controlled_buffer_1
  not not_1 (not_1_out, register_1_q);
  Comparator #(.width(16), .mode("unsigned")) comparator_4 (
    .a(cdm16_1_run), .b(16'h1), .eq(comparator_4_eq));  // open: gt, lt
  Comparator #(.width(16), .mode("unsigned")) comparator_5 (
    .a(cdm16_1_cheker), .b(16'h1), .eq(comparator_5_eq));  // open: gt, lt
  assign Command = register_1_q ? 16'h2 : 16'bz;  // Controlled_Buffer controlled_buffer_2

  // Other names for the same wires on the sheet: clk = clock
endmodule
module newmain2 (
);

  wire abst_obj_1_drawing, clock_1_out, clock_2_out, cmd_show, comparator_1_eq, counter_1_carry, not_1_out,
       not_2_out, not_3_out, or_1_out, pull_resistor_1_node, register_1_q, register_2_q, xor_1_out;
  wire [2:0] p_inp_x;
  wire [3:0] \схема_расчётов_1_p1 , \схема_расчётов_1_p2 ;
  wire [4:0] counter_1_q;
  wire [5:0] abst_obj_1_cur_line;
  wire [6:0] \схема_расчётов_1_p4 , \схема_расчётов_1_p6 ;
  wire [15:0] adder_1_out, bit_extender_1_out, multiplier_1_out, \схема_расчётов_1_p3 , \схема_расчётов_1_p7 ;
  wire [31:0] abst_obj_1_line_x1, abst_obj_1_line_x2, n32video_buffer_extendable_1_out_5,
       n32video_buffer_extendable_1_out_6, n32video_buffer_extendable_1_out_7,
       n32video_buffer_extendable_1_out_8, n32video_buffer_extendable_1_out_9,
       n32video_buffer_extendable_1_out_10, n32video_buffer_extendable_1_out_11,
       n32video_buffer_extendable_1_out_12, n32video_buffer_extendable_1_out_13,
       n32video_buffer_extendable_1_out_14, n32video_buffer_extendable_1_out_15,
       n32video_buffer_extendable_1_out_16, n32video_buffer_extendable_1_out_17,
       n32video_buffer_extendable_1_out_18, n32video_buffer_extendable_1_out_19,
       n32video_buffer_extendable_1_out_20, n32video_buffer_extendable_1_out_21,
       n32video_buffer_extendable_1_out_22, n32video_buffer_extendable_1_out_23,
       n32video_buffer_extendable_1_out_24, n32video_buffer_extendable_1_out_25,
       n32video_buffer_extendable_1_out_26, n32video_buffer_extendable_1_out_27,
       n32video_buffer_extendable_1_out_28, n32video_buffer_extendable_1_out_29,
       n32video_buffer_extendable_1_out_30, n32video_buffer_extendable_1_out_31,
       n32video_buffer_extendable_1_out_32, n32video_buffer_extendable_1_out_33,
       n32video_buffer_extendable_1_out_34, n32video_buffer_extendable_1_out_35,
       n32video_buffer_extendable_1_out_36, rom_1_data;

  Pull_Resistor pull_resistor_1 (.node(pull_resistor_1_node));
  xor xor_1 (xor_1_out, pull_resistor_1_node, register_2_q);
  abst_obj abst_obj_1 (
    .y(\схема_расчётов_1_p6 ), .texture_line(counter_1_q), .write(xor_1_out), .texture_input(rom_1_data),
    .draw(counter_1_carry), .cur_line(abst_obj_1_cur_line), .line_x1(abst_obj_1_line_x1),
    .line_x2(abst_obj_1_line_x2), .x(\схема_расчётов_1_p4 ), .drawing(abst_obj_1_drawing));
  Counter #(.width(5), .max('h3)) counter_1 (
    .Q(counter_1_q), .carry(counter_1_carry), .clk(pull_resistor_1_node), .clr(counter_1_carry));  // open: load, D, count
  Transistor #(.\type ("n"), .gate("br")) transistor_1 (
    .in(clock_1_out), .out(pull_resistor_1_node), .gate(register_2_q));
  Clock clock_1 (.out(clock_1_out));
  Register #(.width(1)) register_1 (
    .D(comparator_1_eq), .Q(register_1_q), .clk(comparator_1_eq), .clr(abst_obj_1_drawing));  // open: en
  Register #(.width(1)) register_2 (
    .D(register_1_q), .Q(register_2_q), .clk(not_1_out), .clr(abst_obj_1_drawing));  // open: en
  not not_1 (not_1_out, clock_2_out);
  Clock clock_2 (.out(clock_2_out));
  or or_1 (or_1_out, register_2_q, register_1_q, abst_obj_1_drawing);
  assign bit_extender_1_out = {{11{1'b0}}, counter_1_q};  // Bit_Extender bit_extender_1
  // Схема_расчётов схема_расчётов_1: pin names not known; wires that end beside it: \схема_расчётов_1_p1 , \схема_расчётов_1_p2 , \схема_расчётов_1_p3 , \схема_расчётов_1_p4 , or_1_out, \схема_расчётов_1_p6 , \схема_расчётов_1_p7 
  Joystick joystick_1 (.x(\схема_расчётов_1_p1 ), .y(\схема_расчётов_1_p2 ));
  // Probe on abst_obj_1_cur_line
  // Probe on \схема_расчётов_1_p3 
  Multiplier #(.width(16)) multiplier_1 (
    .a(\схема_расчётов_1_p3 ), .b(16'h3), .out(multiplier_1_out));  // open: cin, cout
  Comparator #(.width(16), .mode("unsigned")) comparator_1 (
    .a(\схема_расчётов_1_p7 ), .b(16'h1), .eq(comparator_1_eq));  // open: gt, lt
  Comparator #(.width(16), .mode("unsigned")) comparator_2 (
    .a(\схема_расчётов_1_p7 ), .b(16'h2), .eq(cmd_show));  // open: gt, lt
  not not_2 (not_2_out, abst_obj_1_cur_line[5]);
  Adder #(.width(16)) adder_1 (.a(bit_extender_1_out), .b(multiplier_1_out), .out(adder_1_out));  // open: cin, cout
  ROM #(.addrWidth(16), .dataWidth(32)) rom_1 (.addr(adder_1_out), .data(rom_1_data));  // open: sel
  DotMatrix #(.inputtype("row"), .matrixcols(32), .matrixrows(32)) dotmatrix_1 (
    .row0(n32video_buffer_extendable_1_out_5), .row1(n32video_buffer_extendable_1_out_6),
    .row2(n32video_buffer_extendable_1_out_7), .row3(n32video_buffer_extendable_1_out_8),
    .row4(n32video_buffer_extendable_1_out_9), .row5(n32video_buffer_extendable_1_out_10),
    .row6(n32video_buffer_extendable_1_out_11), .row7(n32video_buffer_extendable_1_out_12),
    .row8(n32video_buffer_extendable_1_out_13), .row9(n32video_buffer_extendable_1_out_14),
    .row10(n32video_buffer_extendable_1_out_15), .row11(n32video_buffer_extendable_1_out_16),
    .row12(n32video_buffer_extendable_1_out_17), .row13(n32video_buffer_extendable_1_out_18),
    .row14(n32video_buffer_extendable_1_out_19), .row15(n32video_buffer_extendable_1_out_20),
    .row16(n32video_buffer_extendable_1_out_21), .row17(n32video_buffer_extendable_1_out_22),
    .row18(n32video_buffer_extendable_1_out_23), .row19(n32video_buffer_extendable_1_out_24),
    .row20(n32video_buffer_extendable_1_out_25), .row21(n32video_buffer_extendable_1_out_26),
    .row22(n32video_buffer_extendable_1_out_27), .row23(n32video_buffer_extendable_1_out_28),
    .row24(n32video_buffer_extendable_1_out_29), .row25(n32video_buffer_extendable_1_out_30),
    .row26(n32video_buffer_extendable_1_out_31), .row27(n32video_buffer_extendable_1_out_32),
    .row28(n32video_buffer_extendable_1_out_33), .row29(n32video_buffer_extendable_1_out_34),
    .row30(n32video_buffer_extendable_1_out_35), .row31(n32video_buffer_extendable_1_out_36));
  _32video_buffer_extendable u_32video_buffer_extendable_1 (
    .in_1(abst_obj_1_line_x1), .out_5(n32video_buffer_extendable_1_out_5),
    .out_6(n32video_buffer_extendable_1_out_6), .out_7(n32video_buffer_extendable_1_out_7),
    .out_8(n32video_buffer_extendable_1_out_8), .out_9(n32video_buffer_extendable_1_out_9),
    .out_10(n32video_buffer_extendable_1_out_10), .out_11(n32video_buffer_extendable_1_out_11),
    .out_12(n32video_buffer_extendable_1_out_12), .out_13(n32video_buffer_extendable_1_out_13),
    .out_14(n32video_buffer_extendable_1_out_14), .out_15(n32video_buffer_extendable_1_out_15),
    .out_16(n32video_buffer_extendable_1_out_16), .out_17(n32video_buffer_extendable_1_out_17),
    .out_18(n32video_buffer_extendable_1_out_18), .out_19(n32video_buffer_extendable_1_out_19),
    .out_20(n32video_buffer_extendable_1_out_20), .out_21(n32video_buffer_extendable_1_out_21),
    .out_22(n32video_buffer_extendable_1_out_22), .out_23(n32video_buffer_extendable_1_out_23),
    .out_24(n32video_buffer_extendable_1_out_24), .out_25(n32video_buffer_extendable_1_out_25),
    .out_26(n32video_buffer_extendable_1_out_26), .out_27(n32video_buffer_extendable_1_out_27),
    .out_28(n32video_buffer_extendable_1_out_28), .out_29(n32video_buffer_extendable_1_out_29),
    .out_30(n32video_buffer_extendable_1_out_30), .out_31(n32video_buffer_extendable_1_out_31),
    .out_32(n32video_buffer_extendable_1_out_32), .out_33(n32video_buffer_extendable_1_out_33),
    .out_34(n32video_buffer_extendable_1_out_34), .out_35(n32video_buffer_extendable_1_out_35),
    .out_36(n32video_buffer_extendable_1_out_36), .block(not_3_out), .y(abst_obj_1_cur_line[4:0]),
    .w(cmd_show));
  not not_3 (not_3_out, not_2_out);
  Joystick #(.bits(3)) joystick_2 (.x(p_inp_x));  // open: y

  // Notes on the sheet:
  //   texture line counter
  //   contents of rom_1 (hex, n*v repeats v):
  //   2 7 5 2 5 5 0 0 0 2 7 5 2 5 5 7 5 5 2 7 7 2 5 7 2 5 5
endmodule

module CDM16 (
  input  [15:0] adr,
  input  [15:0] val,
  input  draw,
  input  clock,
  input  write,
  input  hold,
  output [15:0] id,
  output [15:0] x,
  output [15:0] y,
  output [15:0] command,
  output [15:0] collide,
  output [15:0] cheker,
  output [15:0] run
);

  wire and_2_out, and_3_out, and_4_out, and_5_out, and_6_out, and_7_out, and_8_out, and_9_out, and_10_out,
       cdm_16_1_p3, cdm_16_1_p4, code, comparator_1_eq, comparator_3_eq, comparator_4_eq, comparator_5_eq,
       comparator_6_eq, comparator_7_eq, comparator_8_eq, d_ff_1_q, data, draw_t, mem, not_1_out, not_2_out,
       not_3_out, not_4_out, not_5_out, or_1_out, pull_resistor_2_node, pull_resistor_7_node,
       pull_resistor_13_node, read_write, transistor_2_out, transistor_5_out, word, write_t;
  wire [15:0] cdm_16_1_p8, cdm_16_1_p9, cdm_16_1_p10, controlled_buffer_2_out, register_1_q, register_2_q,
       register_3_q, register_4_q, rom_1_p4, transistor_3_out;

  // Debugger debugger_1: pin names not known
  and and_1 (write_t, write, d_ff_1_q);
  D_Flip_Flop d_ff_1 (.clk(not_1_out), .D(or_1_out), .Q(d_ff_1_q));  // open: Qn, preset, en, reset
  not not_1 (not_1_out, clock);
  or or_1 (or_1_out, write, hold);
  // CdM_16 cdm_16_1: pin names not known; wires that end beside it: d_ff_1_q, clock, cdm_16_1_p3, cdm_16_1_p4, mem, read_write, word, cdm_16_1_p8, cdm_16_1_p9, cdm_16_1_p10
  // Probe on cdm_16_1_p3
  not not_2 (not_2_out, write_t);
  not not_3 (not_3_out, write_t);
  assign cdm_16_1_p10 = and_3_out ? controlled_buffer_2_out : 16'bz;  // Controlled_Buffer controlled_buffer_1
  assign controlled_buffer_2_out = and_2_out ? cdm_16_1_p9 : 16'bz;  // Controlled_Buffer controlled_buffer_2
  and and_2 (and_2_out, not_2_out, not_4_out);
  not not_4 (not_4_out, read_write);
  not not_5 (not_5_out, read_write);
  and and_3 (and_3_out, not_3_out, read_write);
  Pull_Resistor pull_resistor_1 (.node(code));
  Transistor #(.gate("br")) transistor_1 (.in(pull_resistor_2_node), .out(data), .gate(write_t));
  Pull_Resistor pull_resistor_2 (.node(pull_resistor_2_node));
  Pull_Resistor #(.pull(1)) pull_resistor_3 (.node(data));
  Decoder decoder_1 (.out0(code), .out1(pull_resistor_2_node), .sel(cdm_16_1_p4), .en(mem));
  Transistor transistor_2 (.in(not_5_out), .out(transistor_2_out), .gate(write_t));
  Pull_Resistor #(.pull(1)) pull_resistor_4 (.node(transistor_2_out));
  Transistor #(.\type ("n"), .width(16)) transistor_3 (.in(adr), .out(transistor_3_out), .gate(write_t));
  Transistor #(.gate("br"), .width(16)) transistor_4 (.in(cdm_16_1_p8), .out(transistor_3_out), .gate(write_t));
  // Probe on transistor_3_out
  Transistor transistor_5 (.in(word), .out(transistor_5_out), .gate(write_t));
  Pull_Resistor pull_resistor_5 (.node(transistor_5_out));
  Comparator #(.width(16)) comparator_1 (.a(transistor_3_out), .b(16'h86), .eq(comparator_1_eq));  // open: gt, lt
  Pull_Resistor pull_resistor_6 (.node(comparator_1_eq));
  Pull_Resistor pull_resistor_7 (.node(pull_resistor_7_node));
  Comparator #(.width(16)) comparator_2 (.a(transistor_3_out), .b(16'h88), .eq(pull_resistor_7_node));  // open: gt, lt
  Comparator #(.width(16)) comparator_3 (.a(transistor_3_out), .b(16'h8a), .eq(comparator_3_eq));  // open: gt, lt
  Pull_Resistor pull_resistor_8 (.node(comparator_3_eq));
  Comparator #(.width(16)) comparator_4 (.a(transistor_3_out), .b(16'h8c), .eq(comparator_4_eq));  // open: gt, lt
  Pull_Resistor pull_resistor_9 (.node(comparator_4_eq));
  Comparator #(.width(16)) comparator_5 (.a(transistor_3_out), .b(16'h94), .eq(comparator_5_eq));  // open: gt, lt
  Pull_Resistor pull_resistor_10 (.node(comparator_5_eq));
  Comparator #(.width(16)) comparator_6 (.a(transistor_3_out), .b(16'h84), .eq(comparator_6_eq));  // open: gt, lt
  Pull_Resistor pull_resistor_11 (.node(comparator_6_eq));
  Comparator #(.width(16)) comparator_7 (.a(transistor_3_out), .b(16'h96), .eq(comparator_7_eq));  // open: gt, lt
  Pull_Resistor pull_resistor_12 (.node(comparator_7_eq));
  Pull_Resistor pull_resistor_13 (.node(pull_resistor_13_node));
  Transistor #(.gate("br")) transistor_6 (.in(read_write), .out(pull_resistor_13_node), .gate(write_t));
  // ROM rom_1: pin names not known; wires that end beside it: transistor_3_out, code, word, rom_1_p4
  // RAM ram_1: pin names not known; wires that end beside it: transistor_3_out, transistor_5_out, data, clock, pull_resistor_13_node, controlled_buffer_2_out
  Register #(.width(16)) register_1 (.D(controlled_buffer_2_out), .Q(register_1_q), .clk(and_4_out));  // open: en, clr
  and and_4 (and_4_out, comparator_1_eq, data, transistor_2_out);
  Register #(.width(16)) register_2 (.D(controlled_buffer_2_out), .Q(register_2_q), .clk(and_5_out));  // open: en, clr
  and and_5 (and_5_out, pull_resistor_7_node, data, transistor_2_out);
  Register #(.width(16)) register_3 (.D(controlled_buffer_2_out), .Q(register_3_q), .clk(and_6_out));  // open: en, clr
  and and_6 (and_6_out, comparator_3_eq, data, transistor_2_out);
  Register #(.width(16)) register_4 (.D(controlled_buffer_2_out), .Q(register_4_q), .clk(and_7_out));  // open: en, clr
  and and_7 (and_7_out, comparator_4_eq, data, transistor_2_out);
  Register #(.width(16)) register_5 (.D(controlled_buffer_2_out), .Q(collide), .clk(and_8_out));  // open: en, clr
  and and_8 (and_8_out, comparator_5_eq, data, transistor_2_out);
  Register #(.width(16)) register_6 (.D(controlled_buffer_2_out), .Q(cheker), .clk(and_9_out));  // open: en, clr
  and and_9 (and_9_out, comparator_6_eq, data, transistor_2_out);
  Register #(.width(16)) register_7 (.D(controlled_buffer_2_out), .Q(run), .clk(and_10_out));  // open: en, clr
  and and_10 (and_10_out, comparator_7_eq, data, transistor_2_out);
  Transistor #(.width(16)) transistor_7 (.in(rom_1_p4), .out(controlled_buffer_2_out), .gate(write_t));
  Transistor #(.\type ("n"), .width(16)) transistor_8 (.in(val), .out(controlled_buffer_2_out), .gate(write_t));
  assign id = draw_t ? register_1_q : 16'bz;  // Controlled_Buffer controlled_buffer_3
  assign x = draw_t ? register_2_q : 16'bz;  // Controlled_Buffer controlled_buffer_4
  assign y = draw_t ? register_3_q : 16'bz;  // Controlled_Buffer controlled_buffer_5
  assign command = draw_t ? register_4_q : 16'bz;  // Controlled_Buffer controlled_buffer_6
  Register #(.width(1)) register_8 (.D(draw), .Q(draw_t), .clk(draw), .clr(comparator_8_eq));  // open: en
  Comparator #(.width(16), .mode("unsigned")) comparator_8 (
    .a(command), .b(16'h2), .eq(comparator_8_eq));  // open: gt, lt

  // Other names for the same wires on the sheet: cl = clock

  // Notes on the sheet:
  //   hold приостанавливает процессор
  //   write как hold но даёт возможность писать в ОЗУ
endmodule

module cheker_write_2 (
  input  [5:0] int_vec,
  input  run,
  input  clock,
  output [15:0] adr,
  output [15:0] val,
  output [5:0] int_vec_2,
  output write,
  output IRQ
);

  wire counter_1_carry, not_1_out, not_2_out, writing;
  wire [1:0] counter_1_q, register_1_q;
  wire [15:0] multiplexer_1_out, multiplexer_2_out;

  Counter #(.width(2), .max('h2)) counter_1 (
    .Q(counter_1_q), .carry(counter_1_carry), .clk(clock), .clr(not_2_out));  // open: load, D, count
  Register #(.width(2)) register_1 (.D(counter_1_q), .Q(register_1_q), .clk(not_1_out), .clr(not_2_out));  // open: en
  not not_1 (not_1_out, clock);
  Multiplexer #(.select(2), .width(16), .enable("false")) multiplexer_1 (
    .in0({16{1'b0}}), .in1(16'h84), .out(multiplexer_1_out), .sel(register_1_q));  // open: in2, in3
  Multiplexer #(.select(2), .width(16), .enable("false")) multiplexer_2 (
    .in0({16{1'b0}}), .in1(16'h2), .out(multiplexer_2_out), .sel(counter_1_q));  // open: in2, in3
  // Probe on multiplexer_1_out
  assign adr = writing ? multiplexer_1_out : 16'bz;  // Controlled_Buffer controlled_buffer_1
  assign val = writing ? multiplexer_2_out : 16'bz;  // Controlled_Buffer controlled_buffer_2
  // Probe on multiplexer_2_out
  not not_2 (not_2_out, writing);
  Transistor #(.\type ("n"), .gate("br")) transistor_1 (.in(writing), .out(write), .gate(writing));
  Register #(.width(1)) register_2 (.D(run), .Q(writing), .clk(run), .clr(counter_1_carry));  // open: en
  assign int_vec_2 = writing ? int_vec : 6'bz;  // Controlled_Buffer controlled_buffer_3
  assign IRQ = writing ? 1'b0 : 1'bz;  // Controlled_Buffer controlled_buffer_4

  // Other names for the same wires on the sheet: clk = clock
endmodule
